// Logisim project s-mips.circ as structural Verilog: 5 circuits, main circuit S-MIPS Board
module S_MIPS_Board (
  output halt
);

  wire button_1_out, CLK, CS, d_ff_1_q, R_W, Reset_out, RST, TTY_EN;
  wire [2:0] KDB;
  wire [3:0] Mask, ram_1_read_time, ram_1_write_time;
  wire [6:0] KDB_DATA, TTY_DATA;
  wire [15:0] Addr;
  wire [31:0] ram_1_data_out_0, ram_1_data_out_1, ram_1_data_out_2, ram_1_data_out_3, s_mips_1_ram_in_0,
       s_mips_1_ram_in_1, s_mips_1_ram_in_2, s_mips_1_ram_in_3;

  TTY #(.rows(25), .cols(80)) tty_1 (.data(TTY_DATA), .clk(CLK), .we(TTY_EN), .clr(RST));
  RAM ram_1 (
    .Address(Addr), .Data_Out_0(ram_1_data_out_0), .Data_Out_1(ram_1_data_out_1),
    .Data_Out_2(ram_1_data_out_2), .Data_Out_3(ram_1_data_out_3), .Data_In_0(s_mips_1_ram_in_0),
    .Data_In_1(s_mips_1_ram_in_1), .Data_In_2(s_mips_1_ram_in_2), .Data_In_3(s_mips_1_ram_in_3), .Mask(Mask),
    .nRead_Write(R_W), .Chip_Select(CS), .Read_Time(ram_1_read_time), .Reset(button_1_out),
    .Write_Time(ram_1_write_time));
  Button button_1 (.out(button_1_out));
  Keyboard #(.buflen(64)) keyboard_1 (.clk(CLK), .re(KDB[0]), .avail(KDB[2]), .data(KDB_DATA));  // open: clr
  S_MIPS s_mips_1 (
    .Kbd_Enable(KDB[0]), .Address(Addr), .Kbd_Clear(KDB[1]), .Kbd_Available(KDB[2]),
    .RAM_In_0(s_mips_1_ram_in_0), .Kbd_ASCII_Data(KDB_DATA), .RAM_In_1(s_mips_1_ram_in_1),
    .TTY_Enable(TTY_EN), .RAM_In_2(s_mips_1_ram_in_2), .RAM_In_3(s_mips_1_ram_in_3),
    .TTY_ASCII_Data(TTY_DATA), .Reset(RST), .RAM_Out_0(ram_1_data_out_0), .Clock(CLK),
    .RAM_Out_1(ram_1_data_out_1), .Stop(halt), .RAM_Out_2(ram_1_data_out_2), .RAM_Out_3(ram_1_data_out_3),
    .Mask(Mask), .Read_Time(ram_1_read_time), .Write_Time(ram_1_write_time), .nRead_Write(R_W),
    .Chip_Select(CS));
  D_Flip_Flop d_ff_1 (.clk(CLK), .D(1'b1), .Q(d_ff_1_q), .reset(Reset_out));  // open: Qn, preset, en
  Button Reset (.out(Reset_out));
  Clock clock_1 (.out(CLK));
  D_Flip_Flop d_ff_2 (.clk(CLK), .D(d_ff_1_q), .Qn(RST), .reset(Reset_out));  // open: Q, preset, en

  // Notes on the sheet:
  //   NO MODIFICAR
  //   Keyboard
endmodule

module RAM (
  input  [15:0] Address,
  input  [31:0] Data_In_0,
  input  [31:0] Data_In_1,
  input  [31:0] Data_In_2,
  input  [31:0] Data_In_3,
  input  [3:0] Mask,
  input  nRead_Write,
  input  Chip_Select,
  input  Reset,
  output [31:0] Data_Out_0,
  output [31:0] Data_Out_1,
  output [31:0] Data_Out_2,
  output [31:0] Data_Out_3,
  output [3:0] Read_Time,
  output [3:0] Write_Time
);

  wire and_2_out, and_3_out, and_4_out, and_5_out, and_6_out, and_7_out, and_8_out, and_9_out, Changed, CLK,
       comparator_2_eq, comparator_3_eq, comparator_4_eq, comparator_5_eq, comparator_6_eq, Count,
       demultiplexer_3_out0, Idle, Idle_q, Load, Load0, Load1, nand_1_out, or_1_out, or_2_out, or_3_out,
       or_4_out, or_5_out, or_6_out, or_7_out, or_8_out, or_9_out, or_10_out, Proc_q, Update_Mem, Zero_Time;
  wire [3:0] counter_1_q, multiplexer_1_out, subtractor_1_out;
  wire [31:0] register_1_q, register_2_q, register_3_q, register_4_q, register_5_q;

  // Probe on 4'b0011
  // Probe on 4'b0101
  Multiplexer #(.width(4), .enable("false")) multiplexer_1 (
    .in0(4'b0011), .in1(4'b0101), .out(multiplexer_1_out), .sel(nRead_Write));
  or or_1 (or_1_out, Idle, Update_Mem);
  or or_2 (or_2_out, ~Chip_Select, Reset);  // OR_Gate
  Subtractor #(.width(4)) subtractor_1 (.a(multiplexer_1_out), .b(4'b0010), .out(subtractor_1_out));  // open: bin, bout
  D_Flip_Flop u_Idle (.clk(CLK), .D(or_1_out), .Q(Idle_q), .preset(or_2_out));  // open: Qn, en, reset
  Demultiplexer #(.enable("false")) demultiplexer_1 (.out0(Idle), .out1(Load0), .in(Idle_q), .sel(Changed));
  // Probe on counter_1_q
  Counter #(.width(4), .max('hf)) counter_1 (
    .load(Load), .D(subtractor_1_out), .count(Count), .Q(counter_1_q), .clk(CLK), .clr(or_3_out));  // open: carry
  or or_3 (or_3_out, ~Chip_Select, Reset);  // OR_Gate
  Comparator #(.width(4), .mode("unsigned")) comparator_1 (
    .a(4'b0000), .b(counter_1_q), .eq(Zero_Time));  // open: gt, lt
  or or_4 (or_4_out, Count, Load0, Load1);
  Register #(.width(32)) register_1 (.D(Data_In_0), .en(Chip_Select), .Q(register_1_q), .clk(CLK), .clr(or_5_out));
  or or_5 (or_5_out, ~Chip_Select, Reset);  // OR_Gate
  Register #(.width(32)) register_2 (.D(Data_In_1), .en(Chip_Select), .Q(register_2_q), .clk(CLK), .clr(or_6_out));
  or or_6 (or_6_out, ~Chip_Select, Reset);  // OR_Gate
  Register #(.width(32)) register_3 (.D(Data_In_2), .en(Chip_Select), .Q(register_3_q), .clk(CLK), .clr(or_7_out));
  or or_7 (or_7_out, ~Chip_Select, Reset);  // OR_Gate
  Register #(.width(32)) register_4 (.D(Data_In_3), .en(Chip_Select), .Q(register_4_q), .clk(CLK), .clr(or_8_out));
  or or_8 (or_8_out, ~Chip_Select, Reset);  // OR_Gate
  Register #(.width(32)) register_5 (
    .D({{11{1'b1}}, nRead_Write, Mask, Address}), .en(Chip_Select), .Q(register_5_q), .clk(CLK),
    .clr(or_9_out));
  or or_9 (or_9_out, ~Chip_Select, Reset);  // OR_Gate
  D_Flip_Flop Proc (.clk(CLK), .D(or_4_out), .Q(Proc_q), .reset(or_10_out));  // open: Qn, preset, en
  or or_10 (or_10_out, ~Chip_Select, Reset);  // OR_Gate
  Demultiplexer #(.enable("false")) demultiplexer_2 (
    .out0(Count), .out1(Update_Mem), .in(demultiplexer_3_out0), .sel(Zero_Time));
  Demultiplexer #(.enable("false")) demultiplexer_3 (
    .out0(demultiplexer_3_out0), .out1(Load1), .in(Proc_q), .sel(Changed));
  Clock clock_1 (.out(CLK));
  Comparator #(.width(32)) comparator_2 (.a(register_1_q), .b(Data_In_0), .eq(comparator_2_eq));  // open: gt, lt
  Comparator #(.width(32)) comparator_3 (.a(register_2_q), .b(Data_In_1), .eq(comparator_3_eq));  // open: gt, lt
  Comparator #(.width(32)) comparator_4 (.a(register_3_q), .b(Data_In_2), .eq(comparator_4_eq));  // open: gt, lt
  Comparator #(.width(32)) comparator_5 (.a(register_4_q), .b(Data_In_3), .eq(comparator_5_eq));  // open: gt, lt
  Comparator #(.width(32)) comparator_6 (
    .a(register_5_q), .b({{11{1'b1}}, nRead_Write, Mask, Address}), .eq(comparator_6_eq));  // open: gt, lt
  nand nand_1 (nand_1_out, comparator_6_eq, comparator_2_eq, comparator_3_eq, comparator_4_eq, comparator_5_eq);
  and and_1 (Changed, nand_1_out, Chip_Select);
  or or_11 (Load, Count, Load1, Load0);
  and and_2 (and_2_out, Mask[0], Update_Mem, nRead_Write);
  and and_3 (and_3_out, Mask[1], Update_Mem, nRead_Write);
  and and_4 (and_4_out, Mask[2], Update_Mem, nRead_Write);
  and and_5 (and_5_out, Mask[3], Update_Mem, nRead_Write);
  RAM_part #(.addrWidth(16), .dataWidth(32), .bus("separate")) ram_1 (
    .addr(Address), .din(Data_In_0), .data(Data_Out_0), .str(and_2_out), .sel(Chip_Select), .clk(CLK),
    .ld(and_6_out), .clr(Reset));
  and and_6 (and_6_out, ~nRead_Write, Idle);  // AND_Gate
  RAM_part #(.addrWidth(16), .dataWidth(32), .bus("separate")) ram_2 (
    .addr(Address), .din(Data_In_1), .data(Data_Out_1), .str(and_3_out), .sel(Chip_Select), .clk(CLK),
    .ld(and_7_out), .clr(Reset));
  and and_7 (and_7_out, ~nRead_Write, Idle);  // AND_Gate
  RAM_part #(.addrWidth(16), .dataWidth(32), .bus("separate")) ram_3 (
    .addr(Address), .din(Data_In_2), .data(Data_Out_2), .str(and_4_out), .sel(Chip_Select), .clk(CLK),
    .ld(and_8_out), .clr(Reset));
  and and_8 (and_8_out, ~nRead_Write, Idle);  // AND_Gate
  RAM_part #(.addrWidth(16), .dataWidth(32), .bus("separate")) ram_4 (
    .addr(Address), .din(Data_In_3), .data(Data_Out_3), .str(and_5_out), .sel(Chip_Select), .clk(CLK),
    .ld(and_9_out), .clr(Reset));
  and and_9 (and_9_out, ~nRead_Write, Idle);  // AND_Gate

  assign Read_Time = 4'b0011;
  assign Write_Time = 4'b0101;

  // Other names for the same wires on the sheet: M0 = Mask[0]; M1 = Mask[1]; M2 = Mask[2]; M3 = Mask[3];
  //   RW = nRead_Write; CLR = Reset; CS = Chip_Select; Load2 = Count

  // Notes on the sheet:
  //   NO MODIFICAR
  //   excepto quizás los valores RT y WT
  //   BANK0
  //   BANK1
  //   BANK2
  //   BANK3
endmodule

module S_MIPS (
  input  Kbd_Available,
  input  [6:0] Kbd_ASCII_Data,
  input  [31:0] RAM_Out_0,
  input  [31:0] RAM_Out_1,
  input  Reset,
  input  [31:0] RAM_Out_2,
  input  Clock,
  input  [31:0] RAM_Out_3,
  input  [3:0] Read_Time,
  input  [3:0] Write_Time,
  output Kbd_Enable,
  output [15:0] Address,
  output Kbd_Clear,
  output TTY_Enable,
  output [6:0] TTY_ASCII_Data,
  output Stop,
  output [31:0] RAM_In_0,
  output [31:0] RAM_In_1,
  output [31:0] RAM_In_2,
  output [31:0] RAM_In_3,
  output [3:0] Mask,
  output nRead_Write,
  output Chip_Select
);


  // Other names for the same wires on the sheet: CLK = Clock; CLR = Reset; CS = Chip_Select;
  //   KBD_AVAIL = Kbd_Available; KBD_CLR = Kbd_Clear; KBD_DATA[6:0] = Kbd_ASCII_Data; RAM_A[15:0] = Address;
  //   RAM_INPUT_0[31:0] = RAM_In_0; RAM_INPUT_1[31:0] = RAM_In_1; RAM_INPUT_2[31:0] = RAM_In_2;
  //   RAM_INPUT_3[31:0] = RAM_In_3; RAM_MASK[3:0] = Mask; RAM_OUTPUT_0[31:0] = RAM_Out_0;
  //   RAM_OUTPUT_1[31:0] = RAM_Out_1; RAM_OUTPUT_2[31:0] = RAM_Out_2; RAM_OUTPUT_3[31:0] = RAM_Out_3;
  //   RW = nRead_Write; TTY_DATA[6:0] = TTY_ASCII_Data

  // Notes on the sheet:
  //   RAM ADDRESS
  //   DATA FROM RAM
  //   DATA TO RAM
  //   DATA WRITE MASK
  //   RAM TIMING
  //   RAM CONTROL
  //   KEYBOARD
  //   TTY
  //   SEQUENCING
endmodule

module ALU (
  input  [31:0] in_1,
  input  [31:0] in_2,
  input  [2:0] in_3,
  input  [1:0] in_4,
  output [31:0] out_5,
  output [31:0] out_6,
  output [31:0] out_7
);

  wire [0:0] Lt, ULt;
  wire [31:0] Add, And, Div_Hi, Div_Lo, Mul_Hi, Mul_Lo, NOR, Or, Sub, UDiv_Hi, UDiv_Lo, UMul_Hi, UMul_Lo, XOR;

  Adder #(.width(32)) adder_1 (.a(in_1), .b(in_2), .out(Add));  // open: cin, cout
  Comparator #(.width(32)) comparator_1 (.a(in_1), .b(in_2), .lt(Lt[0]));  // open: gt, eq
  Multiplier #(.width(32)) multiplier_1 (.a(in_1), .b(in_2), .out(Mul_Lo), .cout(Mul_Hi));  // open: cin
  Multiplier #(.width(32)) multiplier_2 (.a(in_1), .b(in_2), .out(UMul_Lo), .cout(UMul_Hi));  // open: cin
  Subtractor #(.width(32)) subtractor_1 (.a(in_1), .b(in_2), .out(Sub));  // open: bin, bout
  Comparator #(.width(32), .mode("unsigned")) comparator_2 (.a(in_1), .b(in_2), .lt(ULt[0]));  // open: gt, eq
  Divider #(.width(32)) divider_1 (.a(in_1), .b(in_2), .out(Div_Lo), .rem(Div_Hi));  // open: upper
  Divider #(.width(32)) divider_2 (.a(in_1), .b(in_2), .out(UDiv_Lo), .rem(UDiv_Hi));  // open: upper
  assign And = in_1 & in_2;  // AND_Gate and_1, 32 bits wide
  assign Or = in_1 | in_2;  // OR_Gate or_1, 32 bits wide
  assign NOR = ~(in_1 | in_2);  // NOR_Gate nor_1, 32 bits wide
  assign XOR = in_1 ^ in_2;  // XOR_Gate xor_1, 32 bits wide
  Multiplexer #(.select(2), .width(32), .enable("false")) multiplexer_1 (
    .in0(Mul_Lo), .in1(Div_Lo), .in2(UMul_Lo), .in3(UDiv_Lo), .out(out_6), .sel(in_4));
  Multiplexer #(.select(3), .width(32), .enable("false")) multiplexer_2 (
    .in0(Add), .in1(Sub), .in2({{31{1'b0}}, Lt[0]}), .in3({{31{1'b0}}, ULt[0]}), .in4(And), .in5(Or),
    .in6(NOR), .in7(XOR), .out(out_5), .sel(in_3));
  Multiplexer #(.select(2), .width(32), .enable("false")) multiplexer_3 (
    .in0(Mul_Hi), .in1(Div_Hi), .in2(UMul_Hi), .in3(UDiv_Hi), .out(out_7), .sel(in_4));

  // Other names for the same wires on the sheet: A[31:0] = in_1; B[31:0] = in_2; FS[2:0] = in_3;
  //   Mul_Div_UMul_UDiv_Sel[1:0] = in_4; OutAlu[31:0] = out_5; OutHi[31:0] = out_7; OutLo[31:0] = out_6

  // Notes on the sheet:
  //   Function Selector
  //   Inputs
  //   Arithmetic Ops
  //   Mul/UMul/Div/UDiv
  //   Mul/Div/UMul/UDiv Selector
  //   Logic Ops
  //   Selecting Low Output
  //   Outputs
  //   Selcting Output
  //   Selecting Hi Output
endmodule

module RegisterFile (
  input  [31:0] in_1,
  input  [31:0] in_2,
  input  [31:0] in_3,
  input  in_4,
  input  in_5,
  input  [4:0] in_6,
  input  in_7,
  input  in_8,
  input  [4:0] in_9,
  input  in_10,
  input  [4:0] in_11,
  input  in_12,
  output [31:0] out_13,
  output [31:0] out_14,
  output [31:0] out_15,
  output [31:0] out_16,
  output [31:0] out_17
);

  wire E1, E2, E3, E4, E5, E6, E7, E8, E9, E10, E11, E12, E13, E14, E15, E16, E17, E18, E19, E20, E21, E22,
       E23, E24, E25, E26, E27, E28, E29, E30, E31;
  wire [31:0] NewSP, R1, R2, R3, R4, R5, R6, R7, R8, R9, R10, R11, R12, R13, R14, R15, R16, R17, R18, R19,
       R20, R21, R22, R23, R24, R25, R26, R27, R28, R29, R30, R31, SP___4, SP___4_t;

  Demultiplexer #(.select(5), .enable("false")) demultiplexer_1 (
    .out1(E1), .out2(E2), .out3(E3), .out4(E4), .out5(E5), .out6(E6), .out7(E7), .out8(E8), .out9(E9),
    .out10(E10), .out11(E11), .out12(E12), .out13(E13), .out14(E14), .out15(E15), .out16(E16), .out17(E17),
    .out18(E18), .out19(E19), .out20(E20), .out21(E21), .out22(E22), .out23(E23), .out24(E24), .out25(E25),
    .out26(E26), .out27(E27), .out28(E28), .out29(E29), .out30(E30), .out31(E31), .in(in_5), .sel(in_6));  // open: out0
  Register #(.width(32)) register_1 (.D(in_1), .en(E1), .Q(R1), .clk(in_4), .clr(in_7));
  Register #(.width(32)) register_2 (.D(in_1), .en(E2), .Q(R2), .clk(in_4), .clr(in_7));
  Register #(.width(32)) register_3 (.D(in_1), .en(E3), .Q(R3), .clk(in_4), .clr(in_7));
  Register #(.width(32)) register_4 (.D(in_1), .en(E4), .Q(R4), .clk(in_4), .clr(in_7));
  Register #(.width(32)) register_5 (.D(in_1), .en(E5), .Q(R5), .clk(in_4), .clr(in_7));
  Register #(.width(32)) register_6 (.D(in_1), .en(E6), .Q(R6), .clk(in_4), .clr(in_7));
  Register #(.width(32)) register_7 (.D(in_1), .en(E7), .Q(R7), .clk(in_4), .clr(in_7));
  Register #(.width(32)) register_8 (.D(in_3), .en(in_8), .Q(out_16), .clk(in_4), .clr(in_7));
  Register #(.width(32)) register_9 (.D(in_1), .en(E8), .Q(R8), .clk(in_4), .clr(in_7));
  Register #(.width(32)) register_10 (.D(in_1), .en(E9), .Q(R9), .clk(in_4), .clr(in_7));
  Register #(.width(32)) register_11 (.D(in_1), .en(E10), .Q(R10), .clk(in_4), .clr(in_7));
  Register #(.width(32)) register_12 (.D(in_1), .en(E11), .Q(R11), .clk(in_4), .clr(in_7));
  Register #(.width(32)) register_13 (.D(in_1), .en(E12), .Q(R12), .clk(in_4), .clr(in_7));
  Register #(.width(32)) register_14 (.D(in_1), .en(E13), .Q(R13), .clk(in_4), .clr(in_7));
  Register #(.width(32)) register_15 (.D(in_1), .en(E14), .Q(R14), .clk(in_4), .clr(in_7));
  Register #(.width(32)) register_16 (.D(in_1), .en(E15), .Q(R15), .clk(in_4), .clr(in_7));
  Multiplexer #(.select(5), .width(32), .enable("false")) multiplexer_1 (
    .in0({32{1'b0}}), .in1(R1), .in2(R2), .in3(R3), .in4(R4), .in5(R5), .in6(R6), .in7(R7), .in8(R8),
    .in9(R9), .in10(R10), .in11(R11), .in12(R12), .in13(R13), .in14(R14), .in15(R15), .in16(R16), .in17(R17),
    .in18(R18), .in19(R19), .in20(R20), .in21(R21), .in22(R22), .in23(R23), .in24(R24), .in25(R25),
    .in26(R26), .in27(R27), .in28(R28), .in29(R29), .in30(R30), .in31(R31), .out(out_14), .sel(in_11));
  Register #(.width(32)) register_17 (.D(in_2), .en(in_8), .Q(out_17), .clk(in_4), .clr(in_7));
  Register #(.width(32)) register_18 (.D(in_1), .en(E16), .Q(R16), .clk(in_4), .clr(in_7));
  Register #(.width(32)) register_19 (.D(in_1), .en(E17), .Q(R17), .clk(in_4), .clr(in_7));
  Register #(.width(32)) register_20 (.D(in_1), .en(E18), .Q(R18), .clk(in_4), .clr(in_7));
  Register #(.width(32)) register_21 (.D(in_1), .en(E19), .Q(R19), .clk(in_4), .clr(in_7));
  Register #(.width(32)) register_22 (.D(in_1), .en(E20), .Q(R20), .clk(in_4), .clr(in_7));
  Register #(.width(32)) register_23 (.D(in_1), .en(E21), .Q(R21), .clk(in_4), .clr(in_7));
  Register #(.width(32)) register_24 (.D(in_1), .en(E22), .Q(R22), .clk(in_4), .clr(in_7));
  Register #(.width(32)) register_25 (.D(in_1), .en(E23), .Q(R23), .clk(in_4), .clr(in_7));
  Multiplexer #(.select(5), .width(32), .enable("false")) multiplexer_2 (
    .in0({32{1'b0}}), .in1(R1), .in2(R2), .in3(R3), .in4(R4), .in5(R5), .in6(R6), .in7(R7), .in8(R8),
    .in9(R9), .in10(R10), .in11(R11), .in12(R12), .in13(R13), .in14(R14), .in15(R15), .in16(R16), .in17(R17),
    .in18(R18), .in19(R19), .in20(R20), .in21(R21), .in22(R22), .in23(R23), .in24(R24), .in25(R25),
    .in26(R26), .in27(R27), .in28(R28), .in29(R29), .in30(R30), .in31(R31), .out(out_13), .sel(in_9));
  Adder #(.width(32)) adder_1 (.a(out_15), .b(32'h4), .out(SP___4));  // open: cin, cout
  Subtractor #(.width(32)) subtractor_1 (.a(out_15), .b(32'h4), .out(SP___4_t));  // open: bin, bout
  Multiplexer #(.width(32), .enable("false")) multiplexer_3 (.in0(SP___4), .in1(SP___4_t), .out(NewSP), .sel(in_12));
  Register #(.width(32)) register_26 (.D(in_1), .en(E24), .Q(R24), .clk(in_4), .clr(in_7));
  Register #(.width(32)) register_27 (.D(in_1), .en(E25), .Q(R25), .clk(in_4), .clr(in_7));
  Register #(.width(32)) register_28 (.D(in_1), .en(E26), .Q(R26), .clk(in_4), .clr(in_7));
  Register #(.width(32)) register_29 (.D(in_1), .en(E27), .Q(R27), .clk(in_4), .clr(in_7));
  Register #(.width(32)) register_30 (.D(in_1), .en(E28), .Q(R28), .clk(in_4), .clr(in_7));
  Register #(.width(32)) register_31 (.D(in_1), .en(E29), .Q(R29), .clk(in_4), .clr(in_7));
  Register #(.width(32)) register_32 (.D(in_1), .en(E30), .Q(R30), .clk(in_4), .clr(in_7));
  Register #(.width(32)) register_33 (.D(NewSP), .en(in_10), .Q(out_15), .clk(in_4), .clr(in_7));

  // Other names for the same wires on the sheet: A[31:0] = out_13; AS[4:0] = in_9; B[31:0] = out_14; BS[4:0] = in_11;
  //   Clk = in_4; Hi_Input[31:0] = in_2; Hi_Output[31:0] = out_17; Lo_Input[31:0] = in_3; Lo_Output[31:0] = out_16;
  //   NewData[31:0] = in_1; Pop_Push_Sel = in_12; R_W = in_5; R_W_Hi_Lo = in_8; R_W_SP = in_10; Reset = in_7;
  //   RS[4:0] = in_6; SP[31:0] = out_15

  // Notes on the sheet:
  //   Selecting register to write data into
  //   Selecting Low's input/output
  //   Inputs
  //   Operation Selectors
  //   Register Selectors
  //   Writing input to registers
  //   Selection Output
  //   Selecting Hi's input/output
  //   Outputs
  //   Computing SP
endmodule
