// Logisim project s-mips.circ as structural Verilog: 19 circuits, main circuit S-MIPS Board
module S_MIPS_Board (
  output halt
);

  wire button_1_out, CLK, CS, d_ff_1_q, R_W, Reset_out, RST, TTY_EN;
  wire [2:0] KDB;
  wire [3:0] Mask, ram_1_read_time, ram_1_write_time;
  wire [6:0] KDB_DATA, TTY_DATA;
  wire [15:0] Addr;
  wire [31:0] ram_1_data_out_0, ram_1_data_out_1, ram_1_data_out_2, ram_1_data_out_3, s_mips_1_ram_in_0,
       s_mips_1_ram_in_1, s_mips_1_ram_in_2, s_mips_1_ram_in_3;

  TTY #(.rows(25), .cols(80)) tty_1 (.data(TTY_DATA), .clk(CLK), .we(TTY_EN), .clr(RST));
  RAM ram_1 (
    .Address(Addr), .Data_Out_0(ram_1_data_out_0), .Data_Out_1(ram_1_data_out_1),
    .Data_Out_2(ram_1_data_out_2), .Data_Out_3(ram_1_data_out_3), .Data_In_0(s_mips_1_ram_in_0),
    .Data_In_1(s_mips_1_ram_in_1), .Data_In_2(s_mips_1_ram_in_2), .Data_In_3(s_mips_1_ram_in_3), .Mask(Mask),
    .nRead_Write(R_W), .Chip_Select(CS), .Read_Time(ram_1_read_time), .Reset(button_1_out),
    .Write_Time(ram_1_write_time));
  Button button_1 (.out(button_1_out));
  Keyboard #(.buflen(64)) keyboard_1 (.clk(CLK), .re(KDB[0]), .avail(KDB[2]), .data(KDB_DATA));  // open: clr
  S_MIPS s_mips_1 (
    .Kbd_Enable(KDB[0]), .Address(Addr), .Kbd_Clear(KDB[1]), .Kbd_Available(KDB[2]),
    .RAM_In_0(s_mips_1_ram_in_0), .Kbd_ASCII_Data(KDB_DATA), .RAM_In_1(s_mips_1_ram_in_1),
    .TTY_Enable(TTY_EN), .RAM_In_2(s_mips_1_ram_in_2), .RAM_In_3(s_mips_1_ram_in_3),
    .TTY_ASCII_Data(TTY_DATA), .Reset(RST), .RAM_Out_0(ram_1_data_out_0), .Clock(CLK),
    .RAM_Out_1(ram_1_data_out_1), .Stop(halt), .RAM_Out_2(ram_1_data_out_2), .RAM_Out_3(ram_1_data_out_3),
    .Mask(Mask), .Read_Time(ram_1_read_time), .Write_Time(ram_1_write_time), .nRead_Write(R_W),
    .Chip_Select(CS));
  D_Flip_Flop d_ff_1 (.clk(CLK), .D(1'b1), .Q(d_ff_1_q), .reset(Reset_out));  // open: Qn, preset, en
  Button Reset (.out(Reset_out));
  Clock clock_1 (.out(CLK));
  D_Flip_Flop d_ff_2 (.clk(CLK), .D(d_ff_1_q), .Qn(RST), .reset(Reset_out));  // open: Q, preset, en

  // Notes on the sheet:
  //   NO MODIFICAR
  //   Keyboard
endmodule

module RAM (
  input  [15:0] Address,
  input  [31:0] Data_In_0,
  input  [31:0] Data_In_1,
  input  [31:0] Data_In_2,
  input  [31:0] Data_In_3,
  input  [3:0] Mask,
  input  nRead_Write,
  input  Chip_Select,
  input  Reset,
  output [31:0] Data_Out_0,
  output [31:0] Data_Out_1,
  output [31:0] Data_Out_2,
  output [31:0] Data_Out_3,
  output [3:0] Read_Time,
  output [3:0] Write_Time
);

  wire and_2_out, and_3_out, and_4_out, and_5_out, and_6_out, and_7_out, and_8_out, and_9_out, Changed, CLK,
       comparator_2_eq, comparator_3_eq, comparator_4_eq, comparator_5_eq, comparator_6_eq, Count,
       demultiplexer_3_out0, Idle, Idle_q, Load, Load0, Load1, nand_1_out, or_1_out, or_2_out, or_3_out,
       or_4_out, or_5_out, or_6_out, or_7_out, or_8_out, or_9_out, or_10_out, Proc_q, Update_Mem, Zero_Time;
  wire [3:0] counter_1_q, multiplexer_1_out, subtractor_1_out;
  wire [31:0] register_1_q, register_2_q, register_3_q, register_4_q, register_5_q;

  // Probe on 4'b0011
  // Probe on 4'b0101
  Multiplexer #(.width(4), .enable("false")) multiplexer_1 (
    .in0(4'b0011), .in1(4'b0101), .out(multiplexer_1_out), .sel(nRead_Write));
  or or_1 (or_1_out, Idle, Update_Mem);
  or or_2 (or_2_out, ~Chip_Select, Reset);  // OR_Gate
  Subtractor #(.width(4)) subtractor_1 (.a(multiplexer_1_out), .b(4'b0010), .out(subtractor_1_out));  // open: bin, bout
  Demultiplexer #(.enable("false")) demultiplexer_1 (.out0(Idle), .out1(Load0), .in(Idle_q), .sel(Changed));
  D_Flip_Flop u_Idle (.clk(CLK), .D(or_1_out), .Q(Idle_q), .preset(or_2_out));  // open: Qn, en, reset
  // Probe on counter_1_q
  Counter #(.width(4), .max('hf)) counter_1 (
    .load(Load), .D(subtractor_1_out), .count(Count), .Q(counter_1_q), .clk(CLK), .clr(or_3_out));  // open: carry
  or or_3 (or_3_out, ~Chip_Select, Reset);  // OR_Gate
  Comparator #(.width(4), .mode("unsigned")) comparator_1 (
    .a(4'b0000), .b(counter_1_q), .eq(Zero_Time));  // open: gt, lt
  or or_4 (or_4_out, Count, Load0, Load1);
  Register #(.width(32)) register_1 (.D(Data_In_0), .en(Chip_Select), .Q(register_1_q), .clk(CLK), .clr(or_5_out));
  or or_5 (or_5_out, ~Chip_Select, Reset);  // OR_Gate
  Register #(.width(32)) register_2 (.D(Data_In_1), .en(Chip_Select), .Q(register_2_q), .clk(CLK), .clr(or_6_out));
  or or_6 (or_6_out, ~Chip_Select, Reset);  // OR_Gate
  Register #(.width(32)) register_3 (.D(Data_In_2), .en(Chip_Select), .Q(register_3_q), .clk(CLK), .clr(or_7_out));
  or or_7 (or_7_out, ~Chip_Select, Reset);  // OR_Gate
  Register #(.width(32)) register_4 (.D(Data_In_3), .en(Chip_Select), .Q(register_4_q), .clk(CLK), .clr(or_8_out));
  or or_8 (or_8_out, ~Chip_Select, Reset);  // OR_Gate
  Register #(.width(32)) register_5 (
    .D({{11{1'b1}}, nRead_Write, Mask, Address}), .en(Chip_Select), .Q(register_5_q), .clk(CLK),
    .clr(or_9_out));
  or or_9 (or_9_out, ~Chip_Select, Reset);  // OR_Gate
  D_Flip_Flop Proc (.clk(CLK), .D(or_4_out), .Q(Proc_q), .reset(or_10_out));  // open: Qn, preset, en
  or or_10 (or_10_out, ~Chip_Select, Reset);  // OR_Gate
  Demultiplexer #(.enable("false")) demultiplexer_2 (
    .out0(Count), .out1(Update_Mem), .in(demultiplexer_3_out0), .sel(Zero_Time));
  Demultiplexer #(.enable("false")) demultiplexer_3 (
    .out0(demultiplexer_3_out0), .out1(Load1), .in(Proc_q), .sel(Changed));
  Clock clock_1 (.out(CLK));
  Comparator #(.width(32)) comparator_2 (.a(register_1_q), .b(Data_In_0), .eq(comparator_2_eq));  // open: gt, lt
  Comparator #(.width(32)) comparator_3 (.a(register_2_q), .b(Data_In_1), .eq(comparator_3_eq));  // open: gt, lt
  Comparator #(.width(32)) comparator_4 (.a(register_3_q), .b(Data_In_2), .eq(comparator_4_eq));  // open: gt, lt
  Comparator #(.width(32)) comparator_5 (.a(register_4_q), .b(Data_In_3), .eq(comparator_5_eq));  // open: gt, lt
  Comparator #(.width(32)) comparator_6 (
    .a(register_5_q), .b({{11{1'b1}}, nRead_Write, Mask, Address}), .eq(comparator_6_eq));  // open: gt, lt
  nand nand_1 (nand_1_out, comparator_6_eq, comparator_2_eq, comparator_3_eq, comparator_4_eq, comparator_5_eq);
  and and_1 (Changed, nand_1_out, Chip_Select);
  or or_11 (Load, Count, Load1, Load0);
  and and_2 (and_2_out, Mask[0], Update_Mem, nRead_Write);
  and and_3 (and_3_out, Mask[1], Update_Mem, nRead_Write);
  and and_4 (and_4_out, Mask[2], Update_Mem, nRead_Write);
  and and_5 (and_5_out, Mask[3], Update_Mem, nRead_Write);
  RAM_part #(.addrWidth(16), .dataWidth(32), .bus("separate")) ram_1 (
    .addr(Address), .din(Data_In_0), .data(Data_Out_0), .str(and_2_out), .sel(Chip_Select), .clk(CLK),
    .ld(and_6_out), .clr(Reset));
  and and_6 (and_6_out, ~nRead_Write, Idle);  // AND_Gate
  RAM_part #(.addrWidth(16), .dataWidth(32), .bus("separate")) ram_2 (
    .addr(Address), .din(Data_In_1), .data(Data_Out_1), .str(and_3_out), .sel(Chip_Select), .clk(CLK),
    .ld(and_7_out), .clr(Reset));
  and and_7 (and_7_out, ~nRead_Write, Idle);  // AND_Gate
  RAM_part #(.addrWidth(16), .dataWidth(32), .bus("separate")) ram_3 (
    .addr(Address), .din(Data_In_2), .data(Data_Out_2), .str(and_4_out), .sel(Chip_Select), .clk(CLK),
    .ld(and_8_out), .clr(Reset));
  and and_8 (and_8_out, ~nRead_Write, Idle);  // AND_Gate
  RAM_part #(.addrWidth(16), .dataWidth(32), .bus("separate")) ram_4 (
    .addr(Address), .din(Data_In_3), .data(Data_Out_3), .str(and_5_out), .sel(Chip_Select), .clk(CLK),
    .ld(and_9_out), .clr(Reset));
  and and_9 (and_9_out, ~nRead_Write, Idle);  // AND_Gate

  assign Read_Time = 4'b0011;
  assign Write_Time = 4'b0101;

  // Other names for the same wires on the sheet: M0 = Mask[0]; M1 = Mask[1]; M2 = Mask[2]; M3 = Mask[3];
  //   RW = nRead_Write; CLR = Reset; CS = Chip_Select; Load2 = Count

  // Notes on the sheet:
  //   NO MODIFICAR
  //   excepto quizás los valores RT y WT
  //   BANK0
  //   BANK1
  //   BANK2
  //   BANK3
endmodule

module S_MIPS (
  input  Kbd_Available,
  input  [6:0] Kbd_ASCII_Data,
  input  [31:0] RAM_Out_0,
  input  [31:0] RAM_Out_1,
  input  Reset,
  input  [31:0] RAM_Out_2,
  input  Clock,
  input  [31:0] RAM_Out_3,
  input  [3:0] Read_Time,
  input  [3:0] Write_Time,
  output Kbd_Enable,
  output [15:0] Address,
  output Kbd_Clear,
  output TTY_Enable,
  output [6:0] TTY_ASCII_Data,
  output Stop,
  output [31:0] RAM_In_0,
  output [31:0] RAM_In_1,
  output [31:0] RAM_In_2,
  output [31:0] RAM_In_3,
  output [3:0] Mask,
  output nRead_Write,
  output Chip_Select
);

  wire add, addi, AluOp, \and , and_1_out, and_2_out, and_3_out, and_4_out, and_7_out, and_8_out, and_9_out,
       and_10_out, and_11_out, andi, beq, bgtz, blez, bltz, bne, ConstantSelect, controlled_buffer_1_out,
       datacache_1_out_12, DHit, div, divu, EnableDC, EnableIC, EnMemoryInst, Execute, halt, HiLoEn,
       id_1_kbd, id_1_tty, IHit, instructioncache_1_out_10, IpLoad, jr, jump, lw, mfhi, mflo, mul, mulu, nop,
       \nor , not_1_out, not_2_out, not_3_out, not_4_out, not_5_out, not_6_out, \or , or_1_out, or_4_out,
       or_6_out, or_7_out, or_8_out, or_9_out, or_10_out, or_15_out, or_16_out, or_17_out, or_18_out,
       or_20_out, or_21_out, or_22_out, ori, pop, push, \rand , ReadCS, ReadEn, ReadInstEn, ReadRamReady,
       ReadReady, slt, slti, sltiu, sltu, sub, sw, WriteCs, WriteEn, WriteReady, \xor , xori, Zero;
  wire [1:0] aluselector_1_muldivselector;
  wire [2:0] aluselector_1_funselector;
  wire [3:0] RAM_mask_t;
  wire [4:0] RD, RegisterSelector, RS, RT;
  wire [15:0] Constant_offset, ReadAddress, WriteAddres;
  wire [25:0] JumpDest;
  wire [31:0] B, B_, bit_extender_2_out, constant, Data, DataAlu, DCacheOut, Hi, ICacheOut, kbd, Lo,
       MemoryData, NewData, PC, RAMMemoryData, Random, register_1_q, Rhi, Rlo, SP, Word_SP;
  wire [31:7] A;

  and and_1 (and_1_out, WriteReady, WriteEn);
  and and_2 (and_2_out, ReadEn, ReadReady);
  or or_1 (or_1_out, and_1_out, and_2_out);
  MemoryInstruction memoryinstruction_1 (
    .in_1(Clock), .in_2(Reset), .in_3(or_1_out), .in_4(and_3_out), .in_5(push), .in_6(pop), .in_7(lw),
    .in_8(sw), .in_9(SP), .in_10(constant), .in_11({A, TTY_ASCII_Data}), .in_12(B), .out_13(ReadEn),
    .out_14(WriteEn), .out_15(EnableDC), .Data(Data), .Address(Word_SP));
  or or_2 (EnMemoryInst, push, pop, lw, sw);
  and and_3 (and_3_out, Execute, EnMemoryInst);
  not not_1 (not_1_out, Zero);
  assign controlled_buffer_1_out = not_1_out ? Constant_offset[15] : 1'bz;  // Controlled_Buffer controlled_buffer_1
  assign controlled_buffer_1_out = Zero ? 1'b0 : 1'bz;  // Controlled_Buffer controlled_buffer_2
  assign constant = {{16{controlled_buffer_1_out}}, Constant_offset};  // Bit_Extender bit_extender_1
  Decoder #(.select(2)) decoder_1 (
    .out0(Mask[0]), .out1(Mask[1]), .out2(Mask[2]), .out3(Mask[3]), .sel(RAM_mask_t[3:2]));  // open: en
  or or_3 (IpLoad, EnableDC, and_4_out);
  and and_4 (and_4_out, not_2_out, Execute);
  not not_2 (not_2_out, EnMemoryInst);
  // Probe on constant
  assign Address = nRead_Write ? WriteAddres : 16'bz;  // Controlled_Buffer controlled_buffer_3
  assign Address = not_3_out ? ReadAddress : 16'bz;  // Controlled_Buffer controlled_buffer_4
  not not_3 (not_3_out, nRead_Write);
  or or_4 (or_4_out, sltu, sltiu);
  or or_5 (Chip_Select, WriteCs, ReadCS);
  or or_6 (or_6_out, add, addi);
  or or_7 (or_7_out, slt, slti);
  or or_8 (or_8_out, \and , andi);
  or or_9 (or_9_out, \or , ori);
  or or_10 (or_10_out, \xor , xori);
  ControlUnit controlunit_1 (
    .in_1(Clock), .in_2(Reset), .in_3(halt), .in_4(ReadReady), .in_5(IpLoad), .out_6(ReadInstEn),
    .out_7(Execute), .out_8(Stop), .out_9(EnableIC));
  or or_11 (AluOp, or_6_out, sub, or_7_out, or_4_out, or_9_out, \nor , or_10_out, or_8_out);
  or or_12 (HiLoEn, mul, mulu, div, divu);
  assign bit_extender_2_out = {{25{1'b0}}, Kbd_ASCII_Data};  // Bit_Extender bit_extender_2
  AluSelector aluselector_1 (
    .add(or_6_out), .sub(sub), .slt(or_7_out), .sltu(or_4_out), .\and (or_8_out), .\or (or_9_out),
    .\nor (\nor ), .\xor (or_10_out), .mul(mul), .mulu(mulu), .div(div), .divu(divu),
    .FunSelector(aluselector_1_funselector), .MulDivSelector(aluselector_1_muldivselector));
  assign kbd = not_4_out ? {32{1'b1}} : 32'bz;  // Controlled_Buffer controlled_buffer_5
  not not_4 (not_4_out, Kbd_Available);
  assign kbd = Kbd_Available ? bit_extender_2_out : 32'bz;  // Controlled_Buffer controlled_buffer_6
  or or_13 (Zero, andi, ori, xori);
  or or_14 (ConstantSelect, slti, addi, sltiu, Zero);
  // Probe on register_1_q
  assign B_ = not_5_out ? B : 32'bz;  // Controlled_Buffer controlled_buffer_7
  not not_5 (not_5_out, ConstantSelect);
  assign B_ = ConstantSelect ? constant : 32'bz;  // Controlled_Buffer controlled_buffer_8
  // Probe on Constant_offset
  Register #(.width(32)) register_1 (.D(MemoryData), .en(EnableIC), .Q(register_1_q), .clk(Clock));  // open: clr
  ALU alu_1 (
    .in_1({A, TTY_ASCII_Data}), .in_2(B_), .in_3(aluselector_1_funselector),
    .in_4(aluselector_1_muldivselector), .out_5(DataAlu), .out_6(Hi), .out_7(Lo));
  and and_5 (Kbd_Enable, id_1_kbd, Execute);
  // Probe on DataAlu
  Random #(.width(32)) random_1 (.clk(Clock), .next(\rand ), .out(Random));  // open: clr
  and and_6 (TTY_Enable, id_1_tty, Execute);
  ID id_1 (
    .Instruction(register_1_q), .nop(nop), .out_4(RS), .sub(sub), .out_6(Constant_offset), .out_7(RT),
    .add(add), .out_9(RD), .out_10(JumpDest), .mult(mul), .mulu(mulu), .div(div), .divu(divu), .slt(slt),
    .sltu(sltu), .\and (\and ), .\or (\or ), .\nor (\nor ), .\xor (\xor ), .addi(addi), .slti(slti),
    .sltiu(sltiu), .andi(andi), .ori(ori), .xori(xori), .lw(lw), .sw(sw), .pop(pop), .push(push), .beq(beq),
    .bne(bne), .blez(blez), .bgtz(bgtz), .bltz(bltz), .j(jump), .jr(jr), .mfhi(mfhi), .mflo(mflo),
    .halt(halt), .tty(id_1_tty), .rnd(\rand ), .kbd(id_1_kbd));
  // Probe on NewData
  or or_15 (or_15_out, ConstantSelect, lw, sw);
  and and_7 (and_7_out, IpLoad, or_16_out);
  or or_16 (or_16_out, AluOp, pop, lw, mfhi, mflo, \rand , Kbd_Enable);
  assign RegisterSelector = or_15_out ? RT : 5'bz;  // Controlled_Buffer controlled_buffer_9
  and and_8 (and_8_out, or_17_out, EnableDC);
  or or_17 (or_17_out, push, pop);
  PC pc_1 (
    .in_1(JumpDest), .in_2(Constant_offset), .in_3({A, TTY_ASCII_Data}), .in_4(B), .in_5(beq), .in_6(bne),
    .in_7(blez), .in_8(bgtz), .in_9(IpLoad), .in_10(bltz), .in_11(Clock), .in_12(jump), .in_13(jr), .IpOut(PC));
  assign RegisterSelector = not_6_out ? RD : 5'bz;  // Controlled_Buffer controlled_buffer_10
  not not_6 (not_6_out, or_15_out);
  RegisterFile registerfile_1 (
    .in_1(NewData), .in_2(Hi), .in_3(Lo), .in_4(Clock), .in_5(and_7_out), .in_6(RegisterSelector),
    .in_7(Reset), .in_8(HiLoEn), .in_9(RS), .in_10(and_8_out), .in_11(RT), .in_12(push),
    .out_13({A, TTY_ASCII_Data}), .out_14(B), .out_15(SP), .out_16(Rhi), .out_17(Rlo));
  assign MemoryData = ReadRamReady ? RAMMemoryData : 32'bz;  // Controlled_Buffer controlled_buffer_11
  or or_18 (or_18_out, pop, lw);
  and and_9 (and_9_out, or_18_out, Execute);
  RAMReader ramreader_1 (
    .in_1(RAM_Out_0), .in_2(RAM_Out_1), .in_3(RAM_Out_2), .in_4(RAM_Out_3), .in_5(PC), .in_6(Word_SP),
    .in_7(Clock), .in_8(and_9_out), .in_9(Reset), .in_10(or_20_out), .in_11(Read_Time), .out_12(ReadAddress),
    .out_13(RAMMemoryData), .out_14(ReadRamReady), .out_15(ReadCS));
  assign MemoryData = DHit ? DCacheOut : 32'bz;  // Controlled_Buffer controlled_buffer_12
  or or_19 (ReadReady, ReadRamReady, IHit, DHit);
  assign NewData = AluOp ? DataAlu : 32'bz;  // Controlled_Buffer controlled_buffer_13
  assign NewData = Kbd_Enable ? kbd : 32'bz;  // Controlled_Buffer controlled_buffer_14
  or or_20 (or_20_out, ReadEn, ReadInstEn);
  assign MemoryData = IHit ? ICacheOut : 32'bz;  // Controlled_Buffer controlled_buffer_15
  assign NewData = or_21_out ? MemoryData : 32'bz;  // Controlled_Buffer controlled_buffer_16
  or or_21 (or_21_out, lw, pop);
  assign NewData = \rand  ? Random : 32'bz;  // Controlled_Buffer controlled_buffer_17
  RAMWriter ramwriter_1 (
    .Data(Data), .Adress(Word_SP), .in_3(WriteEn), .in_4(Clock), .in_5(Reset), .in_6(Write_Time),
    .out_7(RAM_In_0), .out_8(RAM_mask_t), .out_9(WriteAddres), .out_10(RAM_In_1), .out_11(WriteReady),
    .out_12(WriteCs), .out_14(RAM_In_2), .out_15(RAM_In_3), .out_13(nRead_Write));
  assign NewData = mfhi ? Rhi : 32'bz;  // Controlled_Buffer controlled_buffer_18
  assign NewData = mflo ? Rlo : 32'bz;  // Controlled_Buffer controlled_buffer_19
  or or_22 (or_22_out, ReadRamReady, WriteReady);
  and and_10 (and_10_out, EnableDC, or_22_out);
  DataCache datacache_1 (
    .in_1(RAM_Out_0), .in_2(RAM_Out_1), .in_3(RAM_Out_2), .in_4(RAM_Out_3), .in_5(Word_SP), .in_6(Data),
    .in_7(Clock), .in_8(Reset), .in_9(and_10_out), .in_10(WriteEn), .out_11(DCacheOut),
    .out_12(datacache_1_out_12));
  and and_11 (and_11_out, EnableIC, ReadRamReady);
  InstructionCache instructioncache_1 (
    .in_1(RAM_Out_0), .in_2(RAM_Out_1), .in_3(RAM_Out_2), .in_4(RAM_Out_3), .in_5(PC), .in_6(Clock),
    .in_7(Reset), .in_8(and_11_out), .out_9(ICacheOut), .out_10(instructioncache_1_out_10));
  and and_12 (DHit, datacache_1_out_12, ReadEn);
  and and_13 (IHit, instructioncache_1_out_10, ReadInstEn);

  assign Kbd_Clear = Reset;

  // Other names for the same wires on the sheet: A[6:0] = TTY_ASCII_Data; TTY_DATA[6:0] = TTY_ASCII_Data; CLK = Clock;
  //   CS = Chip_Select; EnableInst = EnableIC; ExecuteEnded = EnableDC; KBD_AVAIL = Kbd_Available; CLR = Reset;
  //   KBD_CLR = Reset; KBD_DATA[6:0] = Kbd_ASCII_Data; offset[31:0] = constant; RAM_A[15:0] = Address;
  //   RAM_INPUT_0[31:0] = RAM_In_0; RAM_INPUT_1[31:0] = RAM_In_1; RAM_INPUT_2[31:0] = RAM_In_2;
  //   RAM_INPUT_3[31:0] = RAM_In_3; RAM_MASK[3:0] = Mask; RAM_OUTPUT_0[31:0] = RAM_Out_0;
  //   RAM_OUTPUT_1[31:0] = RAM_Out_1; RAM_OUTPUT_2[31:0] = RAM_Out_2; RAM_OUTPUT_3[31:0] = RAM_Out_3;
  //   RW = nRead_Write; Write = nRead_Write

  // Notes on the sheet:
  //   RAM ADDRESS
  //   DATA FROM RAM
  //   DATA TO RAM
  //   DATA WRITE MASK
  //   RAM TIMING
  //   RAM CONTROL
  //   KEYBOARD
  //   TTY
  //   SEQUENCING
endmodule

module div (
  input  [31:0] in_1,
  input  [31:0] in_2,
  output [31:0] out_3,
  output [31:0] out_4
);

  wire [31:0] minus_A, minus_B, minus_U_Rem, minus_U_Rem_B, minus_U_Res, minus_U_Res_1, multplexer2_1_out_4,
       multplexer2_2_out_4, U_Rem, U_Rem_B, U_Res, U_Res_1;

  Negator #(.width(32)) negator_1 (.in(in_1), .out(minus_A));
  Negator #(.width(32)) negator_2 (.in(in_2), .out(minus_B));
  Negator #(.width(32)) negator_3 (.in(U_Res), .out(minus_U_Res));
  MultPlexer4 multplexer4_1 (
    .out_6(out_3), .in_2(U_Res), .in_3(minus_U_Res), .in_4(minus_U_Res_1), .in_5(U_Res_1),
    .in_1({in_2[31], in_1[31]}));
  Adder #(.width(32)) adder_1 (.a(32'h1), .b(U_Res), .out(U_Res_1));  // open: cin, cout
  Adder #(.width(32)) adder_2 (.a({32{1'b1}}), .b(minus_U_Res), .out(minus_U_Res_1));  // open: cin, cout
  MultPlexer2 multplexer2_1 (.out_4(multplexer2_1_out_4), .in_2(in_1), .in_3(minus_A), .in_1(in_1[31]));
  MultPlexer2 multplexer2_2 (.out_4(multplexer2_2_out_4), .in_2(in_2), .in_3(minus_B), .in_1(in_2[31]));
  Adder #(.width(32)) adder_3 (.a(minus_B), .b(minus_U_Rem), .out(minus_U_Rem_B));  // open: cin, cout
  Adder #(.width(32)) adder_4 (.a(in_2), .b(U_Rem), .out(U_Rem_B));  // open: cin, cout
  Divider #(.width(32)) divider_1 (
    .a(multplexer2_1_out_4), .b(multplexer2_2_out_4), .out(U_Res), .rem(U_Rem));  // open: upper
  Negator #(.width(32)) negator_4 (.in(U_Rem), .out(minus_U_Rem));
  MultPlexer4 multplexer4_2 (
    .out_6(out_4), .in_2(U_Rem), .in_3(U_Rem), .in_4(U_Rem_B), .in_5(minus_U_Rem_B),
    .in_1({in_2[31], in_1[31]}));

  // Other names for the same wires on the sheet: A[31:0] = in_1; Last_A = in_1[31]; B[31:0] = in_2; Last_B = in_2[31];
  //   Rem[31:0] = out_4; Res[31:0] = out_3

  // Notes on the sheet:
  //   INPUTS
  //   SAVING SIGN BIT
  //   GETTING THE 2's COMPLEMENT OF THE INPUTS
  //   BULDING THE RESULT
  //   OUTPUTS
  //   DIVIDING THE MODULES
  //   BUILDING THE REMAINDER
endmodule

module umul (
  input  [31:0] in_1,
  input  [31:0] in_2,
  output [31:0] out_3,
  output [31:0] out_4
);

  wire C;
  wire [31:0] _4XResHigh, Add, multiplexer_1_out;
  wire [31:2] _4XResLow;
  wire [31:30] ResHigh;

  Multiplexer #(.select(2), .width(32), .enable("false")) multiplexer_1 (
    .in0({32{1'b0}}), .in1(in_2), .in2(in_1), .in3(Add), .out(multiplexer_1_out), .sel({in_2[0], in_1[0]}));
  Adder #(.width(32)) adder_1 (.a({in_1[31:1], 1'b0}), .b({in_2[31:1], 1'b0}), .out(Add), .cin(1'b1));  // open: cout
  Multiplier #(.width(32)) multiplier_1 (
    .a({1'b0, in_1[31:1]}), .b({1'b0, in_2[31:1]}), .out({_4XResHigh[1:0], _4XResLow}),
    .cout({ResHigh, _4XResHigh[31:2]}));  // open: cin
  Adder #(.width(32)) adder_2 (.a(multiplexer_1_out), .b({_4XResLow, 2'b00}), .out(out_3), .cout(C));  // open: cin
  Adder #(.width(32)) adder_3 (.a({32{1'b0}}), .b(_4XResHigh), .out(out_4), .cin(C));  // open: cout

  // Other names for the same wires on the sheet: ResLow[31:0] = {_4XResHigh[1:0], _4XResLow};
  //   ResHigh[29:0] = _4XResHigh[31:2]; A[31:0] = in_1; Add_A[31:1] = in_1[31:1]; Op_A[30:0] = in_1[31:1];
  //   Up_A[30:0] = in_1[31:1]; Add_B[31:1] = in_2[31:1]; B[31:0] = in_2; Op_B[30:0] = in_2[31:1];
  //   Up_B[30:0] = in_2[31:1]; CarrySel[1:0] = {in_2[0], in_1[0]}; Last_A = in_1[0]; Last_B = in_2[0];
  //   RetHigh[31:0] = out_4; RetLow[31:0] = out_3

  // Notes on the sheet:
  //   INPUTS
  //   REDUCING TO 31 BITS
  //   BUILDING RESULT
  //   OUTPUTS
  //   BUILDING AMOUNT TO ADD
  //   BUILDING CARRY SELECTOR
  //   MULTIPLYING
endmodule

module ID (
  input  [31:0] Instruction,
  output nop,
  output sub,
  output [4:0] out_4,
  output add,
  output [15:0] out_6,
  output [4:0] out_7,
  output mult,
  output [4:0] out_9,
  output [25:0] out_10,
  output mulu,
  output div,
  output divu,
  output slt,
  output sltu,
  output \and ,
  output \or ,
  output \nor ,
  output \xor ,
  output addi,
  output slti,
  output sltiu,
  output andi,
  output ori,
  output xori,
  output lw,
  output sw,
  output pop,
  output push,
  output beq,
  output bne,
  output blez,
  output bgtz,
  output bltz,
  output j,
  output jr,
  output mfhi,
  output mflo,
  output halt,
  output tty,
  output rnd,
  output kbd
);

  wire I, R, R0, R1, R2;

  and and_1 (R0, ~Instruction[26], ~Instruction[27], ~Instruction[28], ~Instruction[29], ~Instruction[30], ~Instruction[31]);  // AND_Gate
  and and_2 (R1, Instruction[26], Instruction[27], Instruction[28], Instruction[29], Instruction[30], Instruction[31]);
  and and_3 (R2, ~Instruction[26], ~Instruction[27], ~Instruction[28], Instruction[29], Instruction[30], Instruction[31]);  // AND_Gate
  and and_4 (addi, ~Instruction[26], ~Instruction[27], ~Instruction[28], Instruction[29], ~Instruction[30], ~Instruction[31]);  // AND_Gate
  and and_5 (slti, ~Instruction[26], Instruction[27], ~Instruction[28], Instruction[29], ~Instruction[30], ~Instruction[31]);  // AND_Gate
  and and_6 (sltiu, Instruction[26], Instruction[27], ~Instruction[28], Instruction[29], ~Instruction[30], ~Instruction[31]);  // AND_Gate
  and and_7 (andi, ~Instruction[26], ~Instruction[27], Instruction[28], Instruction[29], ~Instruction[30], ~Instruction[31]);  // AND_Gate
  and and_8 (ori, Instruction[26], ~Instruction[27], Instruction[28], Instruction[29], ~Instruction[30], ~Instruction[31]);  // AND_Gate
  and and_9 (xori, ~Instruction[26], Instruction[27], Instruction[28], Instruction[29], ~Instruction[30], ~Instruction[31]);  // AND_Gate
  and and_10 (lw, Instruction[26], Instruction[27], ~Instruction[28], ~Instruction[29], ~Instruction[30], Instruction[31]);  // AND_Gate
  and and_11 (sw, Instruction[26], Instruction[27], ~Instruction[28], Instruction[29], ~Instruction[30], Instruction[31]);  // AND_Gate
  and and_12 (beq, ~Instruction[26], ~Instruction[27], Instruction[28], ~Instruction[29], ~Instruction[30], ~Instruction[31]);  // AND_Gate
  and and_13 (blez, ~Instruction[26], Instruction[27], Instruction[28], ~Instruction[29], ~Instruction[30], ~Instruction[31]);  // AND_Gate
  and and_14 (bgtz, Instruction[26], Instruction[27], Instruction[28], ~Instruction[29], ~Instruction[30], ~Instruction[31]);  // AND_Gate
  and and_15 (bltz, Instruction[26], ~Instruction[27], ~Instruction[28], ~Instruction[29], ~Instruction[30], ~Instruction[31]);  // AND_Gate
  and and_16 (bne, Instruction[26], ~Instruction[27], Instruction[28], ~Instruction[29], ~Instruction[30], ~Instruction[31]);  // AND_Gate
  and and_17 (j, ~Instruction[26], Instruction[27], ~Instruction[28], ~Instruction[29], ~Instruction[30], ~Instruction[31]);  // AND_Gate
  or or_1 (R, R0, R1, R2);
  or or_2 (I, addi, slti, sltiu, andi, ori, xori, bne, lw, sw, beq, blez, bgtz, bltz);
  and and_18 (nop, R0, ~Instruction[0], ~Instruction[1], ~Instruction[2], ~Instruction[3], ~Instruction[4], ~Instruction[5]);  // AND_Gate
  and and_19 (sub, R0, ~Instruction[0], Instruction[1], ~Instruction[2], ~Instruction[3], ~Instruction[4], Instruction[5]);  // AND_Gate
  and and_20 (add, R0, ~Instruction[0], ~Instruction[1], ~Instruction[2], ~Instruction[3], ~Instruction[4], Instruction[5]);  // AND_Gate
  and and_21 (mult, R0, ~Instruction[0], ~Instruction[1], ~Instruction[2], Instruction[3], Instruction[4], ~Instruction[5]);  // AND_Gate
  and and_22 (mulu, R0, Instruction[0], ~Instruction[1], ~Instruction[2], Instruction[3], Instruction[4], ~Instruction[5]);  // AND_Gate
  and and_23 (div, R0, ~Instruction[0], Instruction[1], ~Instruction[2], Instruction[3], Instruction[4], ~Instruction[5]);  // AND_Gate
  and and_24 (divu, R0, Instruction[0], Instruction[1], ~Instruction[2], Instruction[3], Instruction[4], ~Instruction[5]);  // AND_Gate
  and and_25 (slt, R0, ~Instruction[0], Instruction[1], ~Instruction[2], Instruction[3], ~Instruction[4], Instruction[5]);  // AND_Gate
  and and_26 (sltu, R0, Instruction[0], Instruction[1], ~Instruction[2], Instruction[3], ~Instruction[4], Instruction[5]);  // AND_Gate
  and and_27 (\and , R0, ~Instruction[0], ~Instruction[1], Instruction[2], ~Instruction[3], ~Instruction[4], Instruction[5]);  // AND_Gate
  and and_28 (\or , R0, Instruction[0], ~Instruction[1], Instruction[2], ~Instruction[3], ~Instruction[4], Instruction[5]);  // AND_Gate
  and and_29 (\nor , R0, Instruction[0], Instruction[1], Instruction[2], ~Instruction[3], ~Instruction[4], Instruction[5]);  // AND_Gate
  and and_30 (\xor , R0, ~Instruction[0], ~Instruction[1], ~Instruction[2], Instruction[3], ~Instruction[4], Instruction[5]);  // AND_Gate
  and and_31 (jr, R0, ~Instruction[0], ~Instruction[1], ~Instruction[2], Instruction[3], ~Instruction[4], ~Instruction[5]);  // AND_Gate
  and and_32 (mfhi, R0, ~Instruction[0], ~Instruction[1], ~Instruction[2], ~Instruction[3], Instruction[4], ~Instruction[5]);  // AND_Gate
  and and_33 (mflo, R0, ~Instruction[0], Instruction[1], ~Instruction[2], ~Instruction[3], Instruction[4], ~Instruction[5]);  // AND_Gate
  and and_34 (pop, R2, ~Instruction[0], ~Instruction[1], ~Instruction[2], ~Instruction[3], ~Instruction[4], ~Instruction[5]);  // AND_Gate
  and and_35 (push, R2, Instruction[0], ~Instruction[1], ~Instruction[2], ~Instruction[3], ~Instruction[4], ~Instruction[5]);  // AND_Gate
  and and_36 (halt, R1, Instruction[0], Instruction[1], Instruction[2], Instruction[3], Instruction[4], Instruction[5]);
  and and_37 (tty, R1, Instruction[0], ~Instruction[1], ~Instruction[2], ~Instruction[3], ~Instruction[4], ~Instruction[5]);  // AND_Gate
  and and_38 (rnd, R1, ~Instruction[0], Instruction[1], ~Instruction[2], ~Instruction[3], ~Instruction[4], ~Instruction[5]);  // AND_Gate
  and and_39 (kbd, R1, ~Instruction[0], ~Instruction[1], Instruction[2], ~Instruction[3], ~Instruction[4], ~Instruction[5]);  // AND_Gate

  assign out_4 = Instruction[25:21];
  assign out_6 = Instruction[15:0];
  assign out_7 = Instruction[20:16];
  assign out_9 = Instruction[15:11];
  assign out_10 = Instruction[25:0];

  // Other names for the same wires on the sheet: Constant[15:0] = Instruction[15:0];
  //   FunctCode[5:0] = Instruction[5:0]; JumpDest[25:0] = Instruction[25:0]; OpCode[5:0] = Instruction[31:26];
  //   jump = j; mul = mult; Rd[4:0] = Instruction[15:11]; Rs[4:0] = Instruction[25:21]; Rt[4:0] = Instruction[20:16]
endmodule

module PC (
  input  [25:0] in_1,
  input  [15:0] in_2,
  input  [31:0] in_3,
  input  [31:0] in_4,
  input  in_5,
  input  in_6,
  input  in_7,
  input  in_8,
  input  in_9,
  input  in_10,
  input  in_11,
  input  in_12,
  input  in_13,
  output [31:0] IpOut
);

  wire _0, _0_t, _0_t_t, _0_t_t_t, _0_t_t_t_t, and_1_out, and_2_out, and_3_out, and_4_out, and_5_out,
       not_1_out, not_2_out, not_3_out, not_4_out, not_5_out, not_6_out, not_7_out, not_8_out, sel_IP_4,
       sel_IP_4_offset_star, sel_jump, sel_RS, tunnel, tunnel_t, tunnel_t_t, tunnel_t_t_t, tunnel_t_t_t_t;
  wire [1:0] selector;
  wire [15:0] offset_4;
  wire [31:0] ip, IP_4, IP_4_offset_4;

  not not_1 (not_1_out, tunnel_t_t);
  and and_1 (and_1_out, in_5, tunnel_t_t);
  and and_2 (and_2_out, in_6, not_1_out);
  and and_3 (and_3_out, in_7, _0_t);
  and and_4 (and_4_out, in_8, _0_t_t_t);
  and and_5 (and_5_out, in_10, _0);
  Comparator #(.width(32)) comparator_1 (.a(in_4), .b(in_3), .gt(tunnel_t_t_t), .eq(tunnel_t_t), .lt(tunnel));
  not not_2 (not_2_out, in_12);
  not not_3 (not_3_out, in_13);
  not not_4 (not_4_out, and_1_out);
  not not_5 (not_5_out, and_2_out);
  not not_6 (not_6_out, and_3_out);
  not not_7 (not_7_out, and_4_out);
  not not_8 (not_8_out, and_5_out);
  Comparator #(.width(32)) comparator_2 (.a(in_3), .b({32{1'b0}}), .gt(_0_t_t_t), .eq(_0_t_t), .lt(_0));
  or or_1 (tunnel_t_t_t_t, tunnel_t_t_t, tunnel_t_t);
  or or_2 (tunnel_t, tunnel_t_t, tunnel);
  or or_3 (_0_t_t_t_t, _0_t_t_t, _0_t_t);
  or or_4 (_0_t, _0_t_t, _0);
  and and_6 (selector[0], not_2_out, not_4_out, not_5_out, not_6_out, not_7_out, not_8_out);
  and and_7 (selector[1], not_2_out, not_3_out);
  Adder #(.width(32)) adder_1 (.a(IpOut), .b(32'h4), .out(IP_4));  // open: cin, cout
  Multiplier #(.width(16)) multiplier_1 (.a(in_2), .b(16'h4), .out(offset_4));  // open: cin, cout
  Adder #(.width(32)) adder_2 (.a(IP_4), .b({{16{1'b0}}, offset_4}), .out(IP_4_offset_4));  // open: cin, cout
  Register #(.width(32)) register_1 (.D(ip), .en(in_9), .Q(IpOut), .clk(in_11));  // open: clr
  assign ip = sel_jump ? {IpOut[31:28], in_1, 2'b00} : 32'bz;  // Controlled_Buffer controlled_buffer_1
  assign ip = sel_RS ? in_3 : 32'bz;  // Controlled_Buffer controlled_buffer_2
  assign ip = sel_IP_4_offset_star ? IP_4_offset_4 : 32'bz;  // Controlled_Buffer controlled_buffer_3
  assign ip = sel_IP_4 ? IP_4 : 32'bz;  // Controlled_Buffer controlled_buffer_4
  Decoder #(.select(2), .enable("false")) decoder_1 (
    .out0(sel_jump), .out1(sel_RS), .out2(sel_IP_4_offset_star), .out3(sel_IP_4), .sel(selector));

  // Other names for the same wires on the sheet: beq = in_5; bgtz = in_8; blez = in_7; bltz = in_10; bne = in_6;
  //   clock = in_11; IpLoad = in_9; j = in_12; jr = in_13; jump[31:2] = {IpOut[31:28], in_1}; JumpDest[25:0] = in_1;
  //   offset[15:0] = in_2; RS[31:0] = in_3; RT[31:0] = in_4

  // Notes on the sheet:
  //   INPUTS
  //   SELECTOR
  //   COMPARE
  //   OUTPUT
endmodule

module ALU (
  input  [31:0] in_1,
  input  [31:0] in_2,
  input  [2:0] in_3,
  input  [1:0] in_4,
  output [31:0] out_5,
  output [31:0] out_6,
  output [31:0] out_7
);

  wire SelAdd, SelAnd, SelHi0, SelHi1, SelHi2, SelHi3, SelLo0, SelLo1, SelLo2, SelLo3, SelLt, SelNor, SelOr,
       SelSub, SelUlt, SelXor;
  wire [0:0] Lt, ULt;
  wire [31:0] Add, And, Div_Hi, Div_Lo, Mul_Hi, Mul_Lo, NOR, Or, Sub, UDiv_Hi, UDiv_Lo, UMul_Hi, UMul_Lo, XOR;

  Adder #(.width(32)) adder_1 (.a(in_1), .b(in_2), .out(Add));  // open: cin, cout
  Comparator #(.width(32)) comparator_1 (.a(in_1), .b(in_2), .lt(Lt[0]));  // open: gt, eq
  Multiplier #(.width(32)) multiplier_1 (.a(in_1), .b(in_2), .out(Mul_Lo), .cout(Mul_Hi));  // open: cin
  umul umul_1 (.out_3(UMul_Lo), .out_4(UMul_Hi), .in_1(in_1), .in_2(in_2));
  Subtractor #(.width(32)) subtractor_1 (.a(in_1), .b(in_2), .out(Sub));  // open: bin, bout
  Comparator #(.width(32), .mode("unsigned")) comparator_2 (.a(in_1), .b(in_2), .lt(ULt[0]));  // open: gt, eq
  div div_1 (.out_3(Div_Lo), .out_4(Div_Hi), .in_1(in_1), .in_2(in_2));
  Divider #(.width(32)) divider_1 (.a(in_1), .b(in_2), .out(UDiv_Lo), .rem(UDiv_Hi));  // open: upper
  assign And = in_1 & in_2;  // AND_Gate and_1, 32 bits wide
  assign Or = in_1 | in_2;  // OR_Gate or_1, 32 bits wide
  assign out_5 = SelAdd ? Add : 32'bz;  // Controlled_Buffer controlled_buffer_1
  Decoder #(.select(2), .enable("false")) decoder_1 (
    .out0(SelLo0), .out1(SelLo1), .out2(SelLo2), .out3(SelLo3), .sel(in_4));
  assign NOR = ~(in_1 | in_2);  // NOR_Gate nor_1, 32 bits wide
  assign XOR = in_1 ^ in_2;  // XOR_Gate xor_1, 32 bits wide
  assign out_5 = SelSub ? Sub : 32'bz;  // Controlled_Buffer controlled_buffer_2
  assign out_6 = SelLo0 ? Mul_Lo : 32'bz;  // Controlled_Buffer controlled_buffer_3
  assign out_6 = SelLo1 ? UMul_Lo : 32'bz;  // Controlled_Buffer controlled_buffer_4
  assign out_6 = SelLo2 ? Div_Lo : 32'bz;  // Controlled_Buffer controlled_buffer_5
  assign out_6 = SelLo3 ? UDiv_Lo : 32'bz;  // Controlled_Buffer controlled_buffer_6
  assign out_5 = SelLt ? {{31{1'b0}}, Lt[0]} : 32'bz;  // Controlled_Buffer controlled_buffer_7
  Decoder #(.select(3)) decoder_2 (
    .out0(SelAdd), .out1(SelSub), .out2(SelLt), .out3(SelUlt), .out4(SelAnd), .out5(SelOr), .out6(SelNor),
    .out7(SelXor), .sel(in_3));  // open: en
  assign out_5 = SelUlt ? {{31{1'b0}}, ULt[0]} : 32'bz;  // Controlled_Buffer controlled_buffer_8
  assign out_5 = SelAnd ? And : 32'bz;  // Controlled_Buffer controlled_buffer_9
  assign out_7 = SelHi1 ? UMul_Hi : 32'bz;  // Controlled_Buffer controlled_buffer_10
  Decoder #(.select(2), .enable("false")) decoder_3 (
    .out0(SelHi0), .out1(SelHi1), .out2(SelHi2), .out3(SelHi3), .sel(in_4));
  assign out_5 = SelOr ? Or : 32'bz;  // Controlled_Buffer controlled_buffer_11
  assign out_7 = SelHi0 ? Mul_Hi : 32'bz;  // Controlled_Buffer controlled_buffer_12
  assign out_7 = SelHi2 ? Div_Hi : 32'bz;  // Controlled_Buffer controlled_buffer_13
  assign out_7 = SelHi3 ? UDiv_Hi : 32'bz;  // Controlled_Buffer controlled_buffer_14
  assign out_5 = SelNor ? NOR : 32'bz;  // Controlled_Buffer controlled_buffer_15
  assign out_5 = SelXor ? XOR : 32'bz;  // Controlled_Buffer controlled_buffer_16

  // Other names for the same wires on the sheet: A[31:0] = in_1; B[31:0] = in_2; FS[2:0] = in_3;
  //   Mul_Div_UMul_UDiv_Sel[1:0] = in_4; OutAlu[31:0] = out_5; OutHi[31:0] = out_7; OutLo[31:0] = out_6

  // Notes on the sheet:
  //   Function Selector
  //   Inputs
  //   Arithmetic Ops
  //   Mul/UMul/Div/UDiv
  //   Mul/Div/UMul/UDiv Selector
  //   Logic Ops
  //   Outputs
  //   Selecting Low Output
  //   Selcting Output
  //   Selecting Hi Output
endmodule

module AluSelector (
  input  add,
  input  sub,
  input  slt,
  input  sltu,
  input  \and ,
  input  \or ,
  input  \nor ,
  input  \xor ,
  input  mul,
  input  mulu,
  input  div,
  input  divu,
  output [2:0] FunSelector,
  output [1:0] MulDivSelector
);

  wire not_1_out, not_2_out, not_3_out, not_4_out, not_5_out, not_6_out, not_7_out, not_8_out, not_9_out,
       not_10_out;

  not not_1 (not_1_out, add);
  not not_2 (not_2_out, sub);
  not not_3 (not_3_out, slt);
  not not_4 (not_4_out, sltu);
  not not_5 (not_5_out, \and );
  not not_6 (not_6_out, \or );
  not not_7 (not_7_out, \nor );
  not not_8 (not_8_out, mul);
  not not_9 (not_9_out, mulu);
  not not_10 (not_10_out, div);
  and and_1 (FunSelector[0], not_7_out, not_1_out, not_3_out, not_5_out);
  and and_2 (FunSelector[1], not_1_out, not_2_out, not_5_out, not_6_out);
  and and_3 (FunSelector[2], not_4_out, not_1_out, not_3_out, not_2_out);
  and and_4 (MulDivSelector[0], not_8_out, not_10_out);
  and and_5 (MulDivSelector[1], not_8_out, not_9_out);
endmodule

module RAMReader (
  input  [31:0] in_1,
  input  [31:0] in_2,
  input  [31:0] in_3,
  input  [31:0] in_4,
  input  [31:0] in_5,
  input  [31:0] in_6,
  input  in_7,
  input  in_8,
  input  in_9,
  input  in_10,
  input  [3:0] in_11,
  output [15:0] out_12,
  output [31:0] out_13,
  output out_14,
  output out_15
);

  wire demultiplexer_1_out0, demultiplexer_1_out1, demultiplexer_2_out0, Done, not_1_out, not_2_out,
       not_3_out, not_4_out, or_1_out, or_2_out, or_3_out, or_4_out, reset, Select0, Select1, Select2,
       Select3;
  wire [1:0] Selector;
  wire [3:0] Count_q;

  Counter #(.width(4), .max('hf)) Count (
    .count(out_15), .Q(Count_q), .clk(in_7), .clr(or_1_out));  // open: load, D, carry
  or or_1 (or_1_out, reset, in_9);
  Comparator #(.width(4), .mode("unsigned")) comparator_1 (.a(in_11), .b(Count_q), .lt(Done));  // open: gt, eq
  assign Selector = not_1_out ? in_5[3:2] : 2'bz;  // Controlled_Buffer controlled_buffer_1
  not not_1 (not_1_out, in_8);
  assign out_12 = not_2_out ? in_5[19:4] : 16'bz;  // Controlled_Buffer controlled_buffer_2
  not not_2 (not_2_out, in_8);
  Decoder #(.select(2), .enable("false")) decoder_1 (
    .out0(Select0), .out1(Select1), .out2(Select2), .out3(Select3), .sel(Selector));
  not not_3 (not_3_out, in_10);
  D_Flip_Flop IDLE (.clk(in_7), .D(or_2_out), .Q(reset), .preset(in_9));  // open: Qn, en, reset
  or or_2 (or_2_out, demultiplexer_1_out0, not_3_out, out_14);
  assign Selector = in_8 ? in_6[3:2] : 2'bz;  // Controlled_Buffer controlled_buffer_3
  assign out_12 = in_8 ? in_6[19:4] : 16'bz;  // Controlled_Buffer controlled_buffer_4
  Demultiplexer demultiplexer_1 (
    .out0(demultiplexer_1_out0), .out1(demultiplexer_1_out1), .in(reset), .sel(in_10));  // open: en
  assign {out_13[7:0], out_13[15:8], out_13[23:16], out_13[31:24]} = Select0 ? in_1 : 32'bz;  // Controlled_Buffer controlled_buffer_5
  assign {out_13[7:0], out_13[15:8], out_13[23:16], out_13[31:24]} = Select1 ? in_2 : 32'bz;  // Controlled_Buffer controlled_buffer_6
  assign {out_13[7:0], out_13[15:8], out_13[23:16], out_13[31:24]} = Select2 ? in_3 : 32'bz;  // Controlled_Buffer controlled_buffer_7
  assign {out_13[7:0], out_13[15:8], out_13[23:16], out_13[31:24]} = Select3 ? in_4 : 32'bz;  // Controlled_Buffer controlled_buffer_8
  or or_3 (or_3_out, demultiplexer_2_out0, demultiplexer_1_out1);
  D_Flip_Flop Read (.clk(in_7), .D(or_3_out), .Q(out_15), .reset(or_4_out));  // open: Qn, preset, en
  or or_4 (or_4_out, not_4_out, in_9);
  not not_4 (not_4_out, in_10);
  Demultiplexer demultiplexer_2 (.out0(demultiplexer_2_out0), .out1(out_14), .in(out_15), .sel(Done));  // open: en

  // Other names for the same wires on the sheet: Out[31:0] = out_13;
  //   Read[31:0] = {out_13[7:0], out_13[15:8], out_13[23:16], out_13[31:24]}; Adress[15:0] = out_12; clock = in_7;
  //   CLR = in_9; CS = out_15; inc = out_15; PC[31:0] = in_5; PC_Out[1:0] = in_5[3:2]; PC_Adress[15:0] = in_5[19:4];
  //   pp = in_8; RAM_0[31:0] = in_1; RAM_1[31:0] = in_2; RAM_2[31:0] = in_3; RAM_3[31:0] = in_4; ReadEnable = in_10;
  //   ready = out_14; RT[3:0] = in_11; Word_SP[31:0] = in_6; Word_SP_Out[1:0] = in_6[3:2];
  //   Word_SP_Adress[15:0] = in_6[19:4]

  // Notes on the sheet:
  //   INPUTS
  //   OUTPUTS
endmodule

module RAMWriter (
  input  [31:0] Data,
  input  [31:0] Adress,
  input  in_3,
  input  in_4,
  input  in_5,
  input  [3:0] in_6,
  output [31:0] out_7,
  output [3:0] out_8,
  output [15:0] out_9,
  output [31:0] out_10,
  output out_11,
  output out_12,
  output out_13,
  output [31:0] out_14,
  output [31:0] out_15
);

  wire demultiplexer_1_out0, demultiplexer_1_out1, Done, IDLE_q, or_1_out, or_2_out;
  wire [3:0] Count_q;

  Counter #(.width(4), .max('hf)) Count (
    .load(out_11), .D(4'b0000), .count(out_12), .Q(Count_q), .clk(in_4), .clr(in_5));  // open: carry
  Comparator #(.width(4)) comparator_1 (.a(in_6), .b(Count_q), .lt(Done));  // open: gt, eq
  D_Flip_Flop IDLE (.clk(in_4), .D(or_1_out), .Q(IDLE_q), .preset(in_5));  // open: Qn, en, reset
  or or_1 (or_1_out, demultiplexer_1_out0, out_11);
  Demultiplexer demultiplexer_1 (
    .out0(demultiplexer_1_out0), .out1(demultiplexer_1_out1), .in(IDLE_q), .sel(in_3));  // open: en
  or or_2 (or_2_out, out_13, demultiplexer_1_out1);
  D_Flip_Flop IDLE_2 (.clk(in_4), .D(or_2_out), .Q(out_12), .reset(in_5));  // open: Qn, preset, en
  Demultiplexer demultiplexer_2 (.out0(out_13), .out1(out_11), .in(out_12), .sel(Done));  // open: en

  assign out_8 = Adress[3:0];
  assign out_9 = Adress[19:4];
  assign out_10 = out_7;
  assign out_14 = out_7;
  assign out_15 = out_7;

  // Other names for the same wires on the sheet: mask[3:0] = Adress[3:0]; WriteAdress[15:0] = Adress[19:4];
  //   clock = in_4; CLR = in_5; CS = out_12; inc = out_12; input1[31:0] = out_7; input2[31:0] = out_7;
  //   input3[31:0] = out_7; input4[31:0] = out_7; Read[31:0] = {out_7[7:0], out_7[15:8], out_7[23:16], out_7[31:24]};
  //   ready = out_11; Write = out_13; WriteEnable = in_3; WT[3:0] = in_6

  // Notes on the sheet:
  //   INPUTS
  //   RAM inputs
  //   OUTPUTS
endmodule

module RegisterFile (
  input  [31:0] in_1,
  input  [31:0] in_2,
  input  [31:0] in_3,
  input  in_4,
  input  in_5,
  input  [4:0] in_6,
  input  in_7,
  input  in_8,
  input  [4:0] in_9,
  input  in_10,
  input  [4:0] in_11,
  input  in_12,
  output [31:0] out_13,
  output [31:0] out_14,
  output [31:0] out_15,
  output [31:0] out_16,
  output [31:0] out_17
);

  wire E1, E2, E3, E4, E5, E6, E7, E8, E9, E10, E11, E12, E13, E14, E15, E16, E17, E18, E19, E20, E21, E22,
       E23, E24, E25, E26, E27, E28, E29, E30, E31;
  wire [31:0] NewSP, R1, R2, R3, R4, R5, R6, R7, R8, R9, R10, R11, R12, R13, R14, R15, R16, R17, R18, R19,
       R20, R21, R22, R23, R24, R25, R26, R27, R28, R29, R30, SP___4, SP___4_t;

  // Probe on in_1
  Demultiplexer #(.select(5), .enable("false")) demultiplexer_1 (
    .out1(E1), .out2(E2), .out3(E3), .out4(E4), .out5(E5), .out6(E6), .out7(E7), .out8(E8), .out9(E9),
    .out10(E10), .out11(E11), .out12(E12), .out13(E13), .out14(E14), .out15(E15), .out16(E16), .out17(E17),
    .out18(E18), .out19(E19), .out20(E20), .out21(E21), .out22(E22), .out23(E23), .out24(E24), .out25(E25),
    .out26(E26), .out27(E27), .out28(E28), .out29(E29), .out30(E30), .out31(E31), .in(in_5), .sel(in_6));  // open: out0
  Register #(.width(32)) register_1 (.D(in_1), .en(E1), .Q(R1), .clk(in_4), .clr(in_7));
  Register #(.width(32)) register_2 (.D(in_1), .en(E2), .Q(R2), .clk(in_4), .clr(in_7));
  Register #(.width(32)) register_3 (.D(in_1), .en(E3), .Q(R3), .clk(in_4), .clr(in_7));
  Register #(.width(32)) register_4 (.D(in_1), .en(E4), .Q(R4), .clk(in_4), .clr(in_7));
  Register #(.width(32)) register_5 (.D(in_1), .en(E5), .Q(R5), .clk(in_4), .clr(in_7));
  Register #(.width(32)) register_6 (.D(in_1), .en(E6), .Q(R6), .clk(in_4), .clr(in_7));
  Register #(.width(32)) register_7 (.D(in_1), .en(E7), .Q(R7), .clk(in_4), .clr(in_7));
  // Probe on in_6
  Register #(.width(32)) register_8 (.D(in_3), .en(in_8), .Q(out_16), .clk(in_4), .clr(in_7));
  Register #(.width(32)) register_9 (.D(in_1), .en(E8), .Q(R8), .clk(in_4), .clr(in_7));
  Register #(.width(32)) register_10 (.D(in_1), .en(E9), .Q(R9), .clk(in_4), .clr(in_7));
  Register #(.width(32)) register_11 (.D(in_1), .en(E10), .Q(R10), .clk(in_4), .clr(in_7));
  Register #(.width(32)) register_12 (.D(in_1), .en(E11), .Q(R11), .clk(in_4), .clr(in_7));
  Register #(.width(32)) register_13 (.D(in_1), .en(E12), .Q(R12), .clk(in_4), .clr(in_7));
  Register #(.width(32)) register_14 (.D(in_1), .en(E13), .Q(R13), .clk(in_4), .clr(in_7));
  Register #(.width(32)) register_15 (.D(in_1), .en(E14), .Q(R14), .clk(in_4), .clr(in_7));
  Register #(.width(32)) register_16 (.D(in_1), .en(E15), .Q(R15), .clk(in_4), .clr(in_7));
  RegisterPlexer registerplexer_1 (
    .in_1(in_11), .in_2(R2), .in_3(R3), .in_4({32{1'b0}}), .in_5(R1), .in_6(R6), .in_7(R7), .in_8(R4),
    .in_9(R5), .in_10(R10), .in_11(R11), .in_12(R8), .in_13(R9), .in_14(R14), .in_15(R15), .in_16(R12),
    .in_17(R13), .in_18(R18), .in_19(R19), .in_20(R16), .in_21(R17), .in_22(R22), .in_23(R23), .in_24(R20),
    .in_25(R21), .in_26(R26), .in_27(R27), .in_28(R24), .in_29(R25), .in_30(R30), .in_31(out_15),
    .in_32(R28), .in_33(R29), .out_34(out_14));
  Register #(.width(32)) register_17 (.D(in_2), .en(in_8), .Q(out_17), .clk(in_4), .clr(in_7));
  Register #(.width(32)) register_18 (.D(in_1), .en(E16), .Q(R16), .clk(in_4), .clr(in_7));
  Register #(.width(32)) register_19 (.D(in_1), .en(E17), .Q(R17), .clk(in_4), .clr(in_7));
  Register #(.width(32)) register_20 (.D(in_1), .en(E18), .Q(R18), .clk(in_4), .clr(in_7));
  Register #(.width(32)) register_21 (.D(in_1), .en(E19), .Q(R19), .clk(in_4), .clr(in_7));
  Register #(.width(32)) register_22 (.D(in_1), .en(E20), .Q(R20), .clk(in_4), .clr(in_7));
  Register #(.width(32)) register_23 (.D(in_1), .en(E21), .Q(R21), .clk(in_4), .clr(in_7));
  Register #(.width(32)) register_24 (.D(in_1), .en(E22), .Q(R22), .clk(in_4), .clr(in_7));
  Register #(.width(32)) register_25 (.D(in_1), .en(E23), .Q(R23), .clk(in_4), .clr(in_7));
  RegisterPlexer registerplexer_2 (
    .in_1(in_9), .in_2(R2), .in_3(R3), .in_4({32{1'b0}}), .in_5(R1), .in_6(R6), .in_7(R7), .in_8(R4),
    .in_9(R5), .in_10(R10), .in_11(R11), .in_12(R8), .in_13(R9), .in_14(R14), .in_15(R15), .in_16(R12),
    .in_17(R13), .in_18(R18), .in_19(R19), .in_20(R16), .in_21(R17), .in_22(R22), .in_23(R23), .in_24(R20),
    .in_25(R21), .in_26(R26), .in_27(R27), .in_28(R24), .in_29(R25), .in_30(R30), .in_31(out_15),
    .in_32(R28), .in_33(R29), .out_34(out_13));
  Adder #(.width(32)) adder_1 (.a(out_15), .b(32'h4), .out(SP___4));  // open: cin, cout
  Subtractor #(.width(32)) subtractor_1 (.a(out_15), .b(32'h4), .out(SP___4_t));  // open: bin, bout
  Register #(.width(32)) register_26 (.D(in_1), .en(E24), .Q(R24), .clk(in_4), .clr(in_7));
  Register #(.width(32)) register_27 (.D(in_1), .en(E25), .Q(R25), .clk(in_4), .clr(in_7));
  Register #(.width(32)) register_28 (.D(in_1), .en(E26), .Q(R26), .clk(in_4), .clr(in_7));
  Register #(.width(32)) register_29 (.D(in_1), .en(E27), .Q(R27), .clk(in_4), .clr(in_7));
  Register #(.width(32)) register_30 (.D(in_1), .en(E28), .Q(R28), .clk(in_4), .clr(in_7));
  Register #(.width(32)) register_31 (.D(in_1), .en(E29), .Q(R29), .clk(in_4), .clr(in_7));
  Register #(.width(32)) register_32 (.D(in_1), .en(E30), .Q(R30), .clk(in_4), .clr(in_7));
  Register #(.width(32)) register_33 (.D(NewSP), .en(in_10), .Q(out_15), .clk(in_4), .clr(in_7));
  MultPlexer2 multplexer2_1 (.out_4(NewSP), .in_2(SP___4), .in_3(SP___4_t), .in_1(in_12));

  // Other names for the same wires on the sheet: A[31:0] = out_13; AS[4:0] = in_9; B[31:0] = out_14; BS[4:0] = in_11;
  //   Clk = in_4; Hi_Input[31:0] = in_2; Hi_Output[31:0] = out_17; Lo_Input[31:0] = in_3; Lo_Output[31:0] = out_16;
  //   NewData[31:0] = in_1; Pop_Push_Sel = in_12; R_W = in_5; R_W_Hi_Lo = in_8; R_W_SP = in_10; Reset = in_7;
  //   RS[4:0] = in_6; R31[31:0] = out_15; SP[31:0] = out_15

  // Notes on the sheet:
  //   Selecting Low's input/output
  //   Inputs
  //   Operation Selectors
  //   Register Selectors
  //   Writing input to registers
  //   Selection Output
  //   Selecting Hi's input/output
  //   Outputs
  //   Computing SP
endmodule

module ControlUnit (
  input  in_1,
  input  in_2,
  input  in_3,
  input  in_4,
  input  in_5,
  output out_6,
  output out_7,
  output out_8,
  output out_9
);

  wire demultiplexer_1_out0, demultiplexer_1_out1, demultiplexer_2_out0, demultiplexer_3_out1, Execute_q,
       IDLE_q, or_1_out;

  D_Flip_Flop IDLE (.clk(in_1), .D(demultiplexer_1_out0), .Q(IDLE_q), .preset(in_2));  // open: Qn, en, reset
  Demultiplexer #(.enable("false")) demultiplexer_1 (
    .out0(demultiplexer_1_out0), .out1(demultiplexer_1_out1), .in(IDLE_q), .sel(in_2));
  or or_1 (or_1_out, demultiplexer_2_out0, in_5, demultiplexer_1_out1);
  D_Flip_Flop Read (.clk(in_1), .D(or_1_out), .Q(out_6));  // open: Qn, preset, en, reset
  Demultiplexer #(.enable("false")) demultiplexer_2 (.out0(demultiplexer_2_out0), .out1(out_9), .in(out_6), .sel(in_4));
  Demultiplexer #(.enable("false")) demultiplexer_3 (
    .out0(out_7), .out1(demultiplexer_3_out1), .in(Execute_q), .sel(in_3));
  D_Flip_Flop Execute (.clk(in_1), .D(out_9), .Q(Execute_q), .reset(in_2));  // open: Qn, preset, en
  D_Flip_Flop Read_2 (.clk(in_1), .D(demultiplexer_3_out1), .Q(out_8), .reset(in_2));  // open: Qn, preset, en

  // Other names for the same wires on the sheet: clear = in_2; clock = in_1; EnableInstruction = out_9;
  //   Execute = out_7; ExecuteFinished = in_5; halt = in_3; ReadInstEnable = out_6; ReadReady = in_4; STOP = out_8
endmodule

module MemoryInstruction (
  input  in_1,
  input  in_2,
  input  in_3,
  input  in_4,
  input  in_5,
  input  in_6,
  input  in_7,
  input  in_8,
  input  [31:0] in_9,
  input  [31:0] in_10,
  input  [31:0] in_11,
  input  [31:0] in_12,
  output out_13,
  output out_14,
  output out_15,
  output [31:0] Data,
  output [31:0] Address
);

  wire demultiplexer_1_out0, EnableMem, not_1_out, or_1_out, or_2_out, or_3_out, or_4_out;
  wire [31:0] adder_1_out, subtractor_1_out, TrueSP;

  assign TrueSP = not_1_out ? in_9 : 32'bz;  // Controlled_Buffer controlled_buffer_1
  not not_1 (not_1_out, in_5);
  assign TrueSP = in_5 ? subtractor_1_out : 32'bz;  // Controlled_Buffer controlled_buffer_2
  Subtractor #(.width(32)) subtractor_1 (.a(in_9), .b(32'h4), .out(subtractor_1_out));  // open: bin, bout
  Adder #(.width(32)) adder_1 (.a(in_11), .b(in_10), .out(adder_1_out));  // open: cin, cout
  assign Data = in_5 ? in_11 : 32'bz;  // Controlled_Buffer controlled_buffer_3
  assign Data = in_8 ? in_12 : 32'bz;  // Controlled_Buffer controlled_buffer_4
  or or_1 (or_1_out, in_6, in_7);
  or or_2 (or_2_out, demultiplexer_1_out0, in_4);
  and and_1 (out_13, EnableMem, or_1_out);
  and and_2 (out_14, EnableMem, or_3_out);
  or or_3 (or_3_out, in_8, in_5);
  D_Flip_Flop d_ff_1 (.clk(in_1), .D(or_2_out), .Q(EnableMem), .reset(in_2));  // open: Qn, preset, en
  MultPlexer2 multplexer2_1 (.out_4(Address), .in_2(TrueSP), .in_3(adder_1_out), .in_1(or_4_out));
  or or_4 (or_4_out, in_7, in_8);
  Demultiplexer #(.enable("false")) demultiplexer_1 (
    .out0(demultiplexer_1_out0), .out1(out_15), .in(EnableMem), .sel(in_3));

  // Other names for the same wires on the sheet: Clear = in_2; Clock = in_1; EnableReader = out_13;
  //   EnableWriter = out_14; Execute = in_4; ExecuteEnded = out_15; load = in_7; MemReady = in_3;
  //   Offset[31:0] = in_10; pop = in_6; push = in_5; RS[31:0] = in_11; RT[31:0] = in_12; SP[31:0] = in_9;
  //   store = in_8
endmodule

module InstructionCache (
  input  [31:0] in_1,
  input  [31:0] in_2,
  input  [31:0] in_3,
  input  [31:0] in_4,
  input  [31:0] in_5,
  input  in_6,
  input  in_7,
  input  in_8,
  output [31:0] out_9,
  output out_10
);

  wire comparator_1_eq, S_0, S_1, S_2, S_3, V;
  wire [11:0] OldTag;
  wire [31:0] OUTPUT_0, OUTPUT_1, OUTPUT_2, OUTPUT_3, Read_Cache_t;

  assign {out_9[7:0], out_9[15:8], out_9[23:16], out_9[31:24]} = S_0 ? OUTPUT_0 : 32'bz;  // Controlled_Buffer controlled_buffer_1
  assign {out_9[7:0], out_9[15:8], out_9[23:16], out_9[31:24]} = S_1 ? OUTPUT_1 : 32'bz;  // Controlled_Buffer controlled_buffer_2
  Decoder #(.select(2), .enable("false")) decoder_1 (.out0(S_0), .out1(S_1), .out2(S_2), .out3(S_3), .sel(in_5[3:2]));
  RAM_part #(.addrWidth(4), .dataWidth(32), .bus("separate")) ram_1 (
    .addr(in_5[7:4]), .din(in_1), .data(OUTPUT_0), .str(in_8), .clk(in_6), .ld(1'b1), .clr(in_7));  // open: sel
  RAM_part #(.addrWidth(4), .dataWidth(32), .bus("separate")) ram_2 (
    .addr(in_5[7:4]), .din(in_2), .data(OUTPUT_1), .str(in_8), .clk(in_6), .ld(1'b1), .clr(in_7));  // open: sel
  RAM_part #(.addrWidth(4), .dataWidth(32), .bus("separate")) ram_3 (
    .addr(in_5[7:4]), .din(in_3), .data(OUTPUT_2), .str(in_8), .clk(in_6), .ld(1'b1), .clr(in_7));  // open: sel
  RAM_part #(.addrWidth(4), .dataWidth(32), .bus("separate")) ram_4 (
    .addr(in_5[7:4]), .din(in_4), .data(OUTPUT_3), .str(in_8), .clk(in_6), .ld(1'b1), .clr(in_7));  // open: sel
  Comparator #(.width(12)) comparator_1 (.a(in_5[19:8]), .b(OldTag), .eq(comparator_1_eq));  // open: gt, lt
  assign {out_9[7:0], out_9[15:8], out_9[23:16], out_9[31:24]} = S_2 ? OUTPUT_2 : 32'bz;  // Controlled_Buffer controlled_buffer_3
  assign Read_Cache_t = S_3 ? OUTPUT_3 : 32'bz;  // Controlled_Buffer controlled_buffer_4
  RAM_part #(.addrWidth(4), .dataWidth(12), .bus("separate")) ram_5 (
    .addr(in_5[7:4]), .din(in_5[19:8]), .data(OldTag), .str(in_8), .clk(in_6), .ld(1'b1), .clr(in_7));  // open: sel
  RAM_part #(.addrWidth(4), .dataWidth(1), .bus("separate")) ram_6 (
    .addr(in_5[7:4]), .din(in_8), .data(V), .str(in_8), .clk(in_6), .ld(1'b1), .clr(in_7));  // open: sel
  and and_1 (out_10, comparator_1_eq, V);

  // Other names for the same wires on the sheet: Cache_Hit = out_10; CLK = in_6; CLR = in_7; Enable = in_8;
  //   IAddress[31:0] = in_5; Selector[1:0] = in_5[3:2]; Index[3:0] = in_5[7:4]; Tag[11:0] = in_5[19:8];
  //   RAM_OUTPUT[31:0] = out_9; Read_Cache[31:0] = {out_9[7:0], out_9[15:8], out_9[23:16], out_9[31:24]};
  //   RAM_OUTPUT_0[31:0] = in_1; RAM_OUTPUT_1[31:0] = in_2; RAM_OUTPUT_2[31:0] = in_3; RAM_OUTPUT_3[31:0] = in_4

  // Notes on the sheet:
  //   Bank 0
  //   Bank 1
  //   Bank 2
  //   Bank 3
  //   Tag
  //   Validity
endmodule

module DataCache (
  input  [31:0] in_1,
  input  [31:0] in_2,
  input  [31:0] in_3,
  input  [31:0] in_4,
  input  [31:0] in_5,
  input  [31:0] in_6,
  input  in_7,
  input  in_8,
  input  in_9,
  input  in_10,
  output [31:0] out_11,
  output out_12
);

  wire comparator_1_eq, En0, En1, En2, En3, M_0, M_1, M_2, M_3, not_1_out, not_2_out, not_3_out, not_4_out,
       not_5_out, V;
  wire [11:0] OTag;
  wire [31:0] Data_Bank0, Data_Bank1, Data_Bank2, Data_Bank3, IData0, IData1, IData2, IData3, OUTPUT_0,
       OUTPUT_1, OUTPUT_2, OUTPUT_3, Read_Cache_t;

  RAM_part #(.addrWidth(4), .dataWidth(32), .bus("separate")) ram_1 (
    .addr(in_5[7:4]), .din(Data_Bank0), .data(OUTPUT_0), .str(En0), .clk(in_7), .ld(1'b1), .clr(in_8));  // open: sel
  RAM_part #(.addrWidth(4), .dataWidth(32), .bus("separate")) ram_2 (
    .addr(in_5[7:4]), .din(Data_Bank1), .data(OUTPUT_1), .str(En1), .clk(in_7), .ld(1'b1), .clr(in_8));  // open: sel
  RAM_part #(.addrWidth(4), .dataWidth(32), .bus("separate")) ram_3 (
    .addr(in_5[7:4]), .din(Data_Bank2), .data(OUTPUT_2), .str(En2), .clk(in_7), .ld(1'b1), .clr(in_8));  // open: sel
  RAM_part #(.addrWidth(4), .dataWidth(32), .bus("separate")) ram_4 (
    .addr(in_5[7:4]), .din(Data_Bank3), .data(OUTPUT_3), .str(En3), .clk(in_7), .ld(1'b1), .clr(in_8));  // open: sel
  assign IData0 = M_0 ? {in_6[7:0], in_6[15:8], in_6[23:16], in_6[31:24]} : 32'bz;  // Controlled_Buffer controlled_buffer_1
  assign IData1 = M_1 ? {in_6[7:0], in_6[15:8], in_6[23:16], in_6[31:24]} : 32'bz;  // Controlled_Buffer controlled_buffer_2
  and and_1 (En0, M_0, in_9);
  and and_2 (En1, M_1, in_9);
  assign {out_11[7:0], out_11[15:8], out_11[23:16], out_11[31:24]} = M_0 ? OUTPUT_0 : 32'bz;  // Controlled_Buffer controlled_buffer_3
  assign {out_11[7:0], out_11[15:8], out_11[23:16], out_11[31:24]} = M_1 ? OUTPUT_1 : 32'bz;  // Controlled_Buffer controlled_buffer_4
  assign {out_11[7:0], out_11[15:8], out_11[23:16], out_11[31:24]} = M_2 ? OUTPUT_2 : 32'bz;  // Controlled_Buffer controlled_buffer_5
  assign Read_Cache_t = M_3 ? OUTPUT_3 : 32'bz;  // Controlled_Buffer controlled_buffer_6
  Comparator #(.width(12)) comparator_1 (.a(in_5[19:8]), .b(OTag), .eq(comparator_1_eq));  // open: gt, lt
  assign IData2 = M_2 ? {in_6[7:0], in_6[15:8], in_6[23:16], in_6[31:24]} : 32'bz;  // Controlled_Buffer controlled_buffer_7
  assign IData3 = M_3 ? {in_6[7:0], in_6[15:8], in_6[23:16], in_6[31:24]} : 32'bz;  // Controlled_Buffer controlled_buffer_8
  and and_3 (En2, M_2, in_9);
  and and_4 (En3, M_3, in_9);
  Decoder #(.select(2), .enable("false")) decoder_1 (.out0(M_0), .out1(M_1), .out2(M_2), .out3(M_3), .sel(in_5[3:2]));
  RAM_part #(.addrWidth(4), .dataWidth(12), .bus("separate")) ram_5 (
    .addr(in_5[7:4]), .din(in_5[19:8]), .data(OTag), .str(in_9), .clk(in_7), .ld(1'b1), .clr(in_8));  // open: sel
  RAM_part #(.addrWidth(4), .dataWidth(1), .bus("separate")) ram_6 (
    .addr(in_5[7:4]), .din(in_9), .data(V), .str(in_9), .clk(in_7), .ld(1'b1), .clr(in_8));  // open: sel
  and and_5 (out_12, comparator_1_eq, V, not_1_out);
  not not_1 (not_1_out, in_10);
  assign Data_Bank0 = in_10 ? IData0 : 32'bz;  // Controlled_Buffer controlled_buffer_9
  assign Data_Bank1 = in_10 ? IData1 : 32'bz;  // Controlled_Buffer controlled_buffer_10
  assign Data_Bank0 = not_2_out ? in_1 : 32'bz;  // Controlled_Buffer controlled_buffer_11
  not not_2 (not_2_out, in_10);
  assign Data_Bank1 = not_3_out ? in_2 : 32'bz;  // Controlled_Buffer controlled_buffer_12
  not not_3 (not_3_out, in_10);
  assign Data_Bank2 = in_10 ? IData2 : 32'bz;  // Controlled_Buffer controlled_buffer_13
  assign Data_Bank3 = in_10 ? IData3 : 32'bz;  // Controlled_Buffer controlled_buffer_14
  assign Data_Bank2 = not_4_out ? in_3 : 32'bz;  // Controlled_Buffer controlled_buffer_15
  not not_4 (not_4_out, in_10);
  assign Data_Bank3 = not_5_out ? in_4 : 32'bz;  // Controlled_Buffer controlled_buffer_16
  not not_5 (not_5_out, in_10);
  // also tied to GND on the sheet: En1

  // Other names for the same wires on the sheet: Cache_Hit = out_12; CLK = in_7; CLR = in_8; B1W[7:0] = in_6[31:24];
  //   Data[31:0] = {in_6[7:0], in_6[15:8], in_6[23:16], in_6[31:24]}; Input[31:0] = in_6; B2W[7:0] = in_6[23:16];
  //   B3W[7:0] = in_6[15:8]; B4W[7:0] = in_6[7:0]; Enable = in_9; EnableWriter = in_10; IAddress[31:0] = in_5;
  //   Mask[1:0] = in_5[3:2]; Index[3:0] = in_5[7:4]; Tag[11:0] = in_5[19:8]; B1R[7:0] = out_11[7:0];
  //   Memory_Data[31:0] = out_11; Read_Cache[31:0] = {out_11[7:0], out_11[15:8], out_11[23:16], out_11[31:24]};
  //   B2R[7:0] = out_11[15:8]; B3R[7:0] = out_11[23:16]; B4R[7:0] = out_11[31:24]; RAM_OUTPUT_0[31:0] = in_1;
  //   RAM_OUTPUT_1[31:0] = in_2; RAM_OUTPUT_2[31:0] = in_3; RAM_OUTPUT_3[31:0] = in_4

  // Notes on the sheet:
  //   Bank 0
  //   Bank 1
  //   Bank 2
  //   Bank 3
  //   Tag
  //   Validity
endmodule

module RegisterPlexer (
  input  [4:0] in_1,
  input  [31:0] in_2,
  input  [31:0] in_3,
  input  [31:0] in_4,
  input  [31:0] in_5,
  input  [31:0] in_6,
  input  [31:0] in_7,
  input  [31:0] in_8,
  input  [31:0] in_9,
  input  [31:0] in_10,
  input  [31:0] in_11,
  input  [31:0] in_12,
  input  [31:0] in_13,
  input  [31:0] in_14,
  input  [31:0] in_15,
  input  [31:0] in_16,
  input  [31:0] in_17,
  input  [31:0] in_18,
  input  [31:0] in_19,
  input  [31:0] in_20,
  input  [31:0] in_21,
  input  [31:0] in_22,
  input  [31:0] in_23,
  input  [31:0] in_24,
  input  [31:0] in_25,
  input  [31:0] in_26,
  input  [31:0] in_27,
  input  [31:0] in_28,
  input  [31:0] in_29,
  input  [31:0] in_30,
  input  [31:0] in_31,
  input  [31:0] in_32,
  input  [31:0] in_33,
  output [31:0] out_34
);

  wire w_00, w_01, w_02, w_03, w_04, w_05, w_06, w_07, w_08, w_09, w_10, w_11, w_12, w_13, w_14, w_15, w_16,
       w_17, w_18, w_19, w_20, w_21, w_22, w_23, w_24, w_25, w_26, w_27, w_28, w_29, w_30, w_31;

  Decoder #(.select(5), .enable("false")) decoder_1 (
    .out0(w_00), .out1(w_01), .out2(w_02), .out3(w_03), .out4(w_04), .out5(w_05), .out6(w_06), .out7(w_07),
    .out8(w_08), .out9(w_09), .out10(w_10), .out11(w_11), .out12(w_12), .out13(w_13), .out14(w_14),
    .out15(w_15), .out16(w_16), .out17(w_17), .out18(w_18), .out19(w_19), .out20(w_20), .out21(w_21),
    .out22(w_22), .out23(w_23), .out24(w_24), .out25(w_25), .out26(w_26), .out27(w_27), .out28(w_28),
    .out29(w_29), .out30(w_30), .out31(w_31), .sel(in_1));
  assign out_34 = w_00 ? in_4 : 32'bz;  // Controlled_Buffer controlled_buffer_1
  assign out_34 = w_04 ? in_8 : 32'bz;  // Controlled_Buffer controlled_buffer_2
  assign out_34 = w_08 ? in_12 : 32'bz;  // Controlled_Buffer controlled_buffer_3
  assign out_34 = w_12 ? in_16 : 32'bz;  // Controlled_Buffer controlled_buffer_4
  assign out_34 = w_16 ? in_20 : 32'bz;  // Controlled_Buffer controlled_buffer_5
  assign out_34 = w_20 ? in_24 : 32'bz;  // Controlled_Buffer controlled_buffer_6
  assign out_34 = w_24 ? in_28 : 32'bz;  // Controlled_Buffer controlled_buffer_7
  assign out_34 = w_28 ? in_32 : 32'bz;  // Controlled_Buffer controlled_buffer_8
  assign out_34 = w_01 ? in_5 : 32'bz;  // Controlled_Buffer controlled_buffer_9
  assign out_34 = w_05 ? in_9 : 32'bz;  // Controlled_Buffer controlled_buffer_10
  assign out_34 = w_09 ? in_13 : 32'bz;  // Controlled_Buffer controlled_buffer_11
  assign out_34 = w_13 ? in_17 : 32'bz;  // Controlled_Buffer controlled_buffer_12
  assign out_34 = w_17 ? in_21 : 32'bz;  // Controlled_Buffer controlled_buffer_13
  assign out_34 = w_21 ? in_25 : 32'bz;  // Controlled_Buffer controlled_buffer_14
  assign out_34 = w_25 ? in_29 : 32'bz;  // Controlled_Buffer controlled_buffer_15
  assign out_34 = w_29 ? in_33 : 32'bz;  // Controlled_Buffer controlled_buffer_16
  assign out_34 = w_02 ? in_2 : 32'bz;  // Controlled_Buffer controlled_buffer_17
  assign out_34 = w_06 ? in_6 : 32'bz;  // Controlled_Buffer controlled_buffer_18
  assign out_34 = w_10 ? in_10 : 32'bz;  // Controlled_Buffer controlled_buffer_19
  assign out_34 = w_14 ? in_14 : 32'bz;  // Controlled_Buffer controlled_buffer_20
  assign out_34 = w_18 ? in_18 : 32'bz;  // Controlled_Buffer controlled_buffer_21
  assign out_34 = w_22 ? in_22 : 32'bz;  // Controlled_Buffer controlled_buffer_22
  assign out_34 = w_26 ? in_26 : 32'bz;  // Controlled_Buffer controlled_buffer_23
  assign out_34 = w_30 ? in_30 : 32'bz;  // Controlled_Buffer controlled_buffer_24
  assign out_34 = w_03 ? in_3 : 32'bz;  // Controlled_Buffer controlled_buffer_25
  assign out_34 = w_07 ? in_7 : 32'bz;  // Controlled_Buffer controlled_buffer_26
  assign out_34 = w_11 ? in_11 : 32'bz;  // Controlled_Buffer controlled_buffer_27
  assign out_34 = w_15 ? in_15 : 32'bz;  // Controlled_Buffer controlled_buffer_28
  assign out_34 = w_19 ? in_19 : 32'bz;  // Controlled_Buffer controlled_buffer_29
  assign out_34 = w_23 ? in_23 : 32'bz;  // Controlled_Buffer controlled_buffer_30
  assign out_34 = w_27 ? in_27 : 32'bz;  // Controlled_Buffer controlled_buffer_31
  assign out_34 = w_31 ? in_31 : 32'bz;  // Controlled_Buffer controlled_buffer_32

  // Other names for the same wires on the sheet: Out[31:0] = out_34; R00[31:0] = in_4; R01[31:0] = in_5;
  //   R02[31:0] = in_2; R03[31:0] = in_3; R04[31:0] = in_8; R05[31:0] = in_9; R06[31:0] = in_6; R07[31:0] = in_7;
  //   R08[31:0] = in_12; R09[31:0] = in_13; R10[31:0] = in_10; R11[31:0] = in_11; R12[31:0] = in_16;
  //   R13[31:0] = in_17; R14[31:0] = in_14; R15[31:0] = in_15; R16[31:0] = in_20; R17[31:0] = in_21;
  //   R18[31:0] = in_18; R19[31:0] = in_19; R20[31:0] = in_24; R21[31:0] = in_25; R22[31:0] = in_22;
  //   R23[31:0] = in_23; R24[31:0] = in_28; R25[31:0] = in_29; R26[31:0] = in_26; R27[31:0] = in_27;
  //   R28[31:0] = in_32; R29[31:0] = in_33; R30[31:0] = in_30; R31[31:0] = in_31; Select[4:0] = in_1
endmodule

module MultPlexer2 (
  input  in_1,
  input  [31:0] in_2,
  input  [31:0] in_3,
  output [31:0] out_4
);

  wire L0, L1;

  Decoder #(.enable("false")) decoder_1 (.out0(L0), .out1(L1), .sel(in_1));
  assign out_4 = L0 ? in_2 : 32'bz;  // Controlled_Buffer controlled_buffer_1
  assign out_4 = L1 ? in_3 : 32'bz;  // Controlled_Buffer controlled_buffer_2

  // Other names for the same wires on the sheet: I1[31:0] = in_2; I2[31:0] = in_3; IS = in_1
endmodule

module MultPlexer4 (
  input  [1:0] in_1,
  input  [31:0] in_2,
  input  [31:0] in_3,
  input  [31:0] in_4,
  input  [31:0] in_5,
  output [31:0] out_6
);

  wire L0, L1, L2, L3;

  Decoder #(.select(2), .enable("false")) decoder_1 (.out0(L0), .out1(L1), .out2(L2), .out3(L3), .sel(in_1));
  assign out_6 = L0 ? in_2 : 32'bz;  // Controlled_Buffer controlled_buffer_1
  assign out_6 = L1 ? in_3 : 32'bz;  // Controlled_Buffer controlled_buffer_2
  assign out_6 = L2 ? in_4 : 32'bz;  // Controlled_Buffer controlled_buffer_3
  assign out_6 = L3 ? in_5 : 32'bz;  // Controlled_Buffer controlled_buffer_4

  // Other names for the same wires on the sheet: I1[31:0] = in_2; I2[31:0] = in_3; I3[31:0] = in_4; I4[31:0] = in_5;
  //   IS[1:0] = in_1
endmodule
